// Logisim project cpu24.circ as structural Verilog: 17 circuits, main circuit ◇单周期MIPS
// ll
module \单周期MIPS  (
  input  IR1,
  input  IR2,
  input  IR3,
  output RegWrite,
  output MemWrite,
  output [31:0] PC,
  output [31:0] IR,
  output [31:0] RDin,
  output [31:0] MDin,
  output [31:0] LedData
);

  wire AluSrcB, and_1_out, and_2_out, and_4_out, Beq, Bne, Branch, CLK, clock_2_out, comparator_1_eq,
       comparator_1_lt, comparator_2_eq, d_ff_1_q, Equal, Go, Halt, IR1_t, IR2_t, IR3_t, IRA, IRB, IRC, Jal,
       Jmp, Jr, LED_EN, MemToReg, nand_1_out, RegDst, RST, SignedExt, Syscall, W1, W2, W3;
  wire [3:0] AluOp;
  wire [4:0] multiplexer_4_out, multiplexer_5_out, multiplexer_9_out, multiplexer_11_out, registerfile_1_p6;
  wire [9:0] bit_extender_2_out, bit_extender_5_out;
  wire [12:0] CNT_num;
  wire [15:0] \总周期数 ;
  wire [31:0] adder_2_out, AluResult, bit_extender_1_out, bit_extender_3_out, bit_extender_4_out,
       Imm16Extend32, Imm16Extend32Shift2, MemoryOut, multiplexer_1_out, multiplexer_2_out,
       multiplexer_7_out, multiplexer_12_out, PCin, PCout, PCoutRaw_4, R1, shifter_2_out, shifter_3_out;

  Clock clock_1 ();  // open: out
  Button _1 (.out(IRA));
  Button _2 (.out(IRB));
  Button _3 (.out(IRC));
  Button button_1 (.out(RST));
  Button \u_继续运行  (.out(Go));
  LED led_1 (.in(W1));
  LED led_2 (.in(W2));
  LED led_3 (.in(W3));
  Register #(.width(32)) u_PC (.D(PCin), .en(Halt), .Q(PC), .clk(CLK), .clr(RST));
  Shifter #(.width(32), .shift("lr")) shifter_1 (.in(PC), .\dist (5'b00010), .out(PCout));
  Hex_Digit_Display hex_digit_display_1 (.value(LedData[31:28]));  // open: dp
  D_Flip_Flop #(.trigger("high")) d_ff_1 (.Q(d_ff_1_q));  // open: clk, D, Qn, preset, en, reset
  // Probe on 13'hc
  Adder #(.width(32)) adder_1 (.a(PC), .b(32'h4), .out(PCoutRaw_4));  // open: cin, cout
  assign bit_extender_1_out = {{6{1'b0}}, IR[25:0]};  // Bit_Extender bit_extender_1
  Hex_Digit_Display hex_digit_display_2 (.value(LedData[27:24]));  // open: dp
  Hex_Digit_Display hex_digit_display_3 (.value(LedData[23:20]));  // open: dp
  // Probe on bit_extender_2_out
  Bit_Extender #(.in_width(32), .out_width(10)) bit_extender_2 (.in(PCout), .out(bit_extender_2_out));
  Comparator #(.width(13)) comparator_1 (
    .a(CNT_num), .b(13'hc), .eq(comparator_1_eq), .lt(comparator_1_lt));  // open: gt
  Clock clock_2 (.out(clock_2_out));
  Multiplexer #(.width(32), .enable("false")) multiplexer_1 (
    .in0(PCoutRaw_4), .in1(adder_2_out), .out(multiplexer_1_out), .sel(Branch));
  Adder #(.width(32)) adder_2 (.a(PCoutRaw_4), .b(Imm16Extend32Shift2), .out(adder_2_out));  // open: cin, cout
  Shifter #(.width(32)) shifter_2 (.in(bit_extender_1_out), .\dist (5'b00010), .out(shifter_2_out));
  // Probe on shifter_2_out
  Hex_Digit_Display hex_digit_display_4 (.value(LedData[19:16]));  // open: dp
  Hex_Digit_Display hex_digit_display_5 (.value(LedData[15:12]));  // open: dp
  Counter #(.width(13), .max('h1fff), .ongoal("stay")) counter_1 (
    .count(comparator_1_lt), .Q(CNT_num), .clk(clock_2_out));  // open: load, D, carry, clr
  Multiplexer #(.width(32), .enable("false")) multiplexer_2 (
    .in0(multiplexer_1_out), .in1(shifter_2_out), .out(multiplexer_2_out), .sel(Jmp));
  Shifter #(.width(32)) shifter_3 (.in(R1), .\dist (5'b00010), .out(shifter_3_out));
  Hex_Digit_Display hex_digit_display_6 (.value(LedData[11:8]));  // open: dp
  Hex_Digit_Display hex_digit_display_7 (.value(LedData[7:4]));  // open: dp
  // Probe on \总周期数 
  ROM #(.addrWidth(10), .dataWidth(32)) rom_1 (.addr(bit_extender_2_out), .data(IR));  // open: sel
  nand nand_1 (nand_1_out, d_ff_1_q, comparator_1_eq);
  Multiplexer #(.width(32), .enable("false")) multiplexer_3 (
    .in0(multiplexer_2_out), .in1(shifter_3_out), .out(PCin), .sel(Jr));
  Register #(.width(32)) register_1 (.D(MDin), .en(LED_EN), .Q(LedData), .clk(CLK), .clr(RST));
  Hex_Digit_Display hex_digit_display_8 (.value(LedData[3:0]));  // open: dp
  // Mips_Probe mips_probe_1: pin names not known; wires that end beside it: IR
  assign CLK = nand_1_out ? clock_2_out : 1'bz;  // Controlled_Buffer controlled_buffer_1
  Pull_Resistor #(.pull(1)) pull_resistor_1 (.node(CLK));
  // Probe on PCin
  // Probe on IR[25:21]
  or or_1 (IR1_t, IR1, IRA);
  assign bit_extender_3_out = {{16{1'b0}}, IR[15:0]};  // Bit_Extender bit_extender_3
  assign bit_extender_4_out = {{16{IR[15]}}, IR[15:0]};  // Bit_Extender bit_extender_4
  Comparator #(.width(32)) comparator_2 (.a(R1), .b(32'h22), .eq(comparator_2_eq));  // open: gt, lt
  or or_2 (IR2_t, IR2, IRB);
  Multiplexer #(.width(5), .enable("false")) multiplexer_4 (
    .in0(IR[20:16]), .in1(IR[15:11]), .out(multiplexer_4_out), .sel(RegDst));
  Multiplexer #(.width(5), .enable("false")) multiplexer_5 (
    .in0(multiplexer_4_out), .in1({5{1'b1}}), .out(multiplexer_5_out), .sel(Jal));
  Multiplexer #(.width(32), .enable("false")) multiplexer_6 (
    .in0(bit_extender_3_out), .in1(bit_extender_4_out), .out(Imm16Extend32), .sel(SignedExt));
  Shifter #(.width(32)) shifter_4 (.in(bit_extender_4_out), .\dist (5'b00010), .out(Imm16Extend32Shift2));
  Multiplexer #(.width(32), .enable("false")) multiplexer_7 (
    .in0(AluResult), .in1(MemoryOut), .out(multiplexer_7_out), .sel(MemToReg));
  and and_1 (and_1_out, Equal, Beq);
  and and_2 (and_2_out, Bne, ~Equal);  // AND_Gate
  and and_3 (LED_EN, comparator_2_eq, Syscall);
  and and_4 (and_4_out, Syscall, ~comparator_2_eq);  // AND_Gate
  // Probe on Imm16Extend32Shift2
  Multiplexer #(.width(32), .enable("false")) multiplexer_8 (
    .in0(multiplexer_7_out), .in1(PCoutRaw_4), .out(RDin), .sel(Jal));
  or or_3 (Branch, and_1_out, and_2_out);
  not not_1 (Halt, and_4_out);
  or or_4 (IR3_t, IR3, IRC);
  Multiplexer #(.width(5), .enable("false")) multiplexer_9 (
    .in0(IR[25:21]), .in1(5'b00010), .out(multiplexer_9_out), .sel(Syscall));
  // RegisterFile registerfile_1: pin names not known; wires that end beside it: RDin, CLK, RegWrite, multiplexer_5_out, multiplexer_9_out, registerfile_1_p6, R1, MDin
  Multiplexer #(.width(5), .enable("false")) multiplexer_10 (
    .in0(IR[20:16]), .in1(5'b00100), .out(registerfile_1_p6), .sel(Syscall));
  // Probe on R1
  // Probe on MDin
  \单周期硬布线控制器  \u_单周期硬布线控制器_1  (
    .Func(IR[5:0]), .OP(IR[31:26]), .ALU_OP(AluOp), .MemToReg(MemToReg), .MemWrite(MemWrite),
    .ALU_SRC(AluSrcB), .RegWrite(RegWrite), .SysCALL(Syscall), .SignedExt(SignedExt), .RegDst(RegDst),
    .JR(Jr), .JMP(Jmp), .Beq(Beq), .JAL(Jal), .Bne(Bne));
  Multiplexer #(.width(5), .enable("false")) multiplexer_11 (
    .in0(IR[20:16]), .in1(IR[15:11]), .out(multiplexer_11_out), .sel(RegDst));
  // MIPS_Regifile mips_regifile_1: pin names not known; wires that end beside it: IR[25:21], IR[20:16], multiplexer_11_out, RDin, RegWrite, CLK, R1, MDin
  Bit_Extender #(.in_width(32), .out_width(10)) bit_extender_5 (.in(AluResult), .out(bit_extender_5_out));
  Multiplexer #(.width(32), .enable("false")) multiplexer_12 (
    .in0(MDin), .in1(Imm16Extend32), .out(multiplexer_12_out), .sel(AluSrcB));
  RAM #(.addrWidth(10), .dataWidth(32), .bus("separate")) ram_1 (
    .addr(bit_extender_5_out), .din(MDin), .data(MemoryOut), .str(MemWrite), .clk(CLK), .clr(RST));  // open: sel, ld
  // Probe on AluOp
  MIPS_ALU mips_alu_1 (
    .X(R1), .Y(multiplexer_12_out), .AluOP(AluOp), .Equal(Equal), .Result(AluResult), .shamt(IR[10:6]));  // open: Result_2
  // Probe on AluResult

  // Other names for the same wires on the sheet: Func[5:0] = IR[5:0]; Imm16[15:0] = IR[15:0]; Imm26[25:0] = IR[25:0];
  //   shamt[4:0] = IR[10:6]; rd[4:0] = IR[15:11]; rt[4:0] = IR[20:16]; rs[4:0] = IR[25:21]; OP[5:0] = IR[31:26];
  //   PCoutRaw[31:0] = PC; R2[31:0] = MDin; WriteBackData[31:0] = RDin

  // Notes on the sheet:
  //   中断源
  //   中断等待指示
  //   总复位信号应将除ROM以外所有存储组件全部清零
  //   控制位
  //   暂停节拍，不能为0
  //   戳工具置1进入计数暂停模式，ctrl+k时钟自动运行到对应节拍暂停
  //   ctrl+k关闭时钟连续运行，将控制位置零，进入单步调试模式调试
  //   用这个时钟源需要去掉电路中的其他时钟源
  //   数码管输出
  //   指令存储器
  //   数码管输出应该用寄存器锁存，否则显示数据只能一闪而过
  //   contents of rom_1 (hex, n*v repeats v):
  //   20110001 8000c05 20110001 20120002 20130003 8000c09 20110001 20120002 20130003 8000c0d 20110001
  //   20120002 20130003 8000c11 20110001 20120002 20130003 c000cb8 20100001 20110001 118fc0 112020
  //   20020022 c 118882 12200001 8000c15 112020 20020022 c 20110001 118880 112020 20020022 c 12200001
  //   8000c1f 20110001 118fc0 112020 20020022 c 1188c3 112020 20020022 c 118903 112020 20020022 c 118903
  //   112020 20020022 c 118903 112020 20020022 c 118903 112020 20020022 c 118903 112020 20020022 c 118903
  //   112020 20020022 c 118903 112020 20020022 c 20100001 109fc0 139fc3 8021 2012000c 24160003 26100001
  //   3210000f 20080008 20090001 139900 2709825 132020 20020022 c 1094022 1500fff9 22100001 2018000f
  //   2188024 108700 20080008 20090001 139902 2709825 132021 20020022 c 1094022 1500fff9 108702 2c9b022
  //   12c00001 8000c50 4020 1084027 84400 3508ffff 82021 20020022 c 2010ffff 20110000 ae300000 22100001
  //   22310004 ae300000 22100001 22310004 ae300000 22100001 22310004 ae300000 22100001 22310004 ae300000
  //   22100001 22310004 ae300000 22100001 22310004 ae300000 22100001 22310004 ae300000 22100001 22310004
  //   ae300000 22100001 22310004 ae300000 22100001 22310004 ae300000 22100001 22310004 ae300000 22100001
  //   22310004 ae300000 22100001 22310004 ae300000 22100001 22310004 ae300000 22100001 22310004 ae300000
  //   22100001 22310004 22100001 8020 2011003c 8e130000 8e340000 274402a 11000002 ae330000 ae140000
  //   2231fffc 1611fff8 102020 20020022 c 22100004 2011003c 1611fff2 20020032 c 20100000 22100001 102020
  //   20020022 c 22100002 102020 20020022 c 22100003 102020 20020022 c 22100004 102020 20020022 c 22100005
  //   102020 20020022 c 22100006 102020 20020022 c 22100007 102020 20020022 c 22100008 102020 20020022
  //   20020022 c 3e00008
  //   OP
  //   Func
  //   rs
  //   指令字
  //   rt
  //   rd
  //   可计数暂停的时钟源
  //   JMP
  //   JR
  //   OP
  //   Func
  //   Beq
  //   Bne
  //   MemToReg
  //   MemWrite
  //   AluOP
  //   AluSrcB
  //   RegWrite
  //   JAL
  //   RegDst
  //   Syscall
  //   为方便自动评测，需要输出PC，IR，寄存器堆写如数据RDin
  //   RAM写使能MemWrite、RAM写入数据MDin等信号
endmodule

// 单周期硬布线控制器
module \单周期硬布线控制器  (
  input  [5:0] OP,
  input  [5:0] Func,
  output [3:0] ALU_OP,
  output MemToReg,
  output MemWrite,
  output ALU_SRC,
  output RegWrite,
  output SysCALL,
  output SignedExt,
  output RegDst,
  output Beq,
  output Bne,
  output JR,
  output JMP,
  output JAL
);

  \运算控制器自动生成  \u_运算控制器自动生成_1  (
    .OP0(OP[0]), .OP1(OP[1]), .OP2(OP[2]), .OP3(OP[3]), .OP4(OP[4]), .OP5(OP[5]), .F0(Func[0]), .F1(Func[1]),
    .F2(Func[2]), .F3(Func[3]), .F4(Func[4]), .F5(Func[5]), .S0(ALU_OP[0]), .S1(ALU_OP[1]), .S2(ALU_OP[2]),
    .S3(ALU_OP[3]));
  \控制信号自动生成  \u_控制信号自动生成_1  (
    .OP0(OP[0]), .OP1(OP[1]), .OP2(OP[2]), .OP3(OP[3]), .OP4(OP[4]), .OP5(OP[5]), .F0(Func[0]), .F1(Func[1]),
    .F2(Func[2]), .F3(Func[3]), .F4(Func[4]), .F5(Func[5]), .MemToReg(MemToReg), .MemWrite(MemWrite),
    .ALU_SRC(ALU_SRC), .RegWrite(RegWrite), .SysCALL(SysCALL), .SignedExt(SignedExt), .RegDst(RegDst),
    .BEQ(Beq), .BNE(Bne), .JR(JR), .JUMP(JMP), .JAL(JAL));

  // Other names for the same wires on the sheet: OP_CODE[5:0] = OP

  // Notes on the sheet:
  //   运算器控制器，根据指令生成运算器功能选择信号
  //   控制信号生成，产生数据通路需要的其他控制信号
endmodule

// 运算器控制器
module \运算控制器自动生成  (
  input  OP0,
  input  OP1,
  input  OP2,
  input  OP3,
  input  OP4,
  input  OP5,
  input  F0,
  input  F1,
  input  F2,
  input  F3,
  input  F4,
  input  F5,
  output S0,
  output S1,
  output S2,
  output S3
);

  wire and_1_out, and_2_out, and_3_out, and_4_out, and_5_out, and_6_out, and_7_out, and_8_out, and_9_out,
       and_10_out, and_11_out, and_12_out, and_13_out, and_14_out, and_15_out, and_16_out, and_17_out,
       and_18_out, and_19_out, and_20_out, and_21_out, and_22_out, and_23_out, and_24_out, and_25_out,
       not_1_out, not_2_out, not_3_out, not_4_out, not_5_out, not_6_out, not_7_out, not_8_out, not_9_out,
       not_10_out, not_11_out, not_12_out, not_13_out, not_14_out, not_15_out, not_16_out, not_17_out,
       not_18_out, not_19_out, not_20_out, not_21_out, not_22_out, not_23_out, not_24_out, not_25_out,
       not_26_out, not_27_out, not_28_out, not_29_out, not_30_out, not_31_out, not_32_out, not_33_out,
       not_34_out, not_35_out, not_36_out, not_37_out, not_38_out, not_39_out, not_40_out, not_41_out,
       not_42_out, not_43_out, not_44_out, not_45_out, not_46_out, not_47_out, not_48_out, not_49_out,
       not_50_out, not_51_out, not_52_out, not_53_out, not_54_out, not_55_out, not_56_out, not_57_out,
       not_58_out, not_59_out, not_60_out, not_61_out, not_62_out, not_63_out, not_64_out, not_65_out,
       not_66_out, not_67_out, not_68_out, not_69_out, not_70_out, not_71_out, not_72_out, not_73_out,
       not_74_out, not_75_out, not_76_out, not_77_out, not_78_out, not_79_out, not_80_out, not_81_out,
       not_82_out, not_83_out, not_84_out, not_85_out, not_86_out, not_87_out, not_88_out, not_89_out,
       not_90_out, not_91_out, not_92_out, not_93_out, not_94_out, not_95_out, not_96_out, not_97_out,
       not_98_out, not_99_out, not_100_out, not_101_out, not_102_out, not_103_out, not_104_out, not_105_out,
       not_106_out, not_107_out, not_108_out, not_109_out, not_110_out, not_111_out, not_112_out,
       not_113_out, not_114_out, not_115_out, not_116_out, not_117_out, not_118_out, not_119_out,
       not_120_out, not_121_out, not_122_out, not_123_out, not_124_out, not_125_out, not_126_out,
       not_127_out, not_128_out, not_129_out, not_130_out, not_131_out, not_132_out, not_133_out,
       not_134_out, not_135_out, not_136_out, not_137_out, not_138_out, not_139_out, not_140_out,
       not_141_out, not_142_out, not_143_out, not_144_out, not_145_out, not_146_out, not_147_out,
       not_148_out, not_149_out, not_150_out, not_151_out, not_152_out, not_153_out, not_154_out,
       not_155_out, not_156_out, not_157_out, not_158_out, not_159_out, not_160_out, not_161_out;

  not not_1 (not_1_out, OP0);
  not not_2 (not_2_out, OP1);
  not not_3 (not_3_out, OP2);
  not not_4 (not_4_out, OP4);
  not not_5 (not_5_out, OP5);
  not not_6 (not_6_out, F0);
  not not_7 (not_7_out, F1);
  not not_8 (not_8_out, F3);
  not not_9 (not_9_out, F4);
  not not_10 (not_10_out, OP0);
  not not_11 (not_11_out, OP1);
  not not_12 (not_12_out, OP2);
  not not_13 (not_13_out, OP4);
  not not_14 (not_14_out, OP5);
  not not_15 (not_15_out, F1);
  not not_16 (not_16_out, F2);
  not not_17 (not_17_out, F3);
  not not_18 (not_18_out, F4);
  not not_19 (not_19_out, OP0);
  not not_20 (not_20_out, OP1);
  not not_21 (not_21_out, OP2);
  not not_22 (not_22_out, OP4);
  not not_23 (not_23_out, OP5);
  not not_24 (not_24_out, F0);
  not not_25 (not_25_out, F2);
  not not_26 (not_26_out, F4);
  not not_27 (not_27_out, OP0);
  not not_28 (not_28_out, OP1);
  not not_29 (not_29_out, OP2);
  not not_30 (not_30_out, OP4);
  not not_31 (not_31_out, OP5);
  not not_32 (not_32_out, F2);
  not not_33 (not_33_out, F3);
  not not_34 (not_34_out, F4);
  not not_35 (not_35_out, F5);
  not not_36 (not_36_out, OP0);
  not not_37 (not_37_out, OP1);
  not not_38 (not_38_out, OP4);
  not not_39 (not_39_out, OP5);
  not not_40 (not_40_out, OP0);
  not not_41 (not_41_out, OP2);
  not not_42 (not_42_out, OP4);
  not not_43 (not_43_out, OP5);
  not not_44 (not_44_out, OP1);
  not not_45 (not_45_out, OP2);
  not not_46 (not_46_out, OP4);
  not not_47 (not_47_out, OP5);
  not not_48 (not_48_out, OP2);
  not not_49 (not_49_out, OP4);
  not not_50 (not_50_out, OP0);
  not not_51 (not_51_out, OP1);
  not not_52 (not_52_out, OP2);
  not not_53 (not_53_out, OP3);
  not not_54 (not_54_out, OP4);
  not not_55 (not_55_out, OP5);
  not not_56 (not_56_out, F0);
  not not_57 (not_57_out, F1);
  not not_58 (not_58_out, F3);
  not not_59 (not_59_out, F4);
  not not_60 (not_60_out, OP0);
  not not_61 (not_61_out, OP1);
  not not_62 (not_62_out, OP2);
  not not_63 (not_63_out, OP3);
  not not_64 (not_64_out, OP4);
  not not_65 (not_65_out, OP5);
  not not_66 (not_66_out, F0);
  not not_67 (not_67_out, F2);
  not not_68 (not_68_out, F3);
  not not_69 (not_69_out, F4);
  not not_70 (not_70_out, OP0);
  not not_71 (not_71_out, OP1);
  not not_72 (not_72_out, OP2);
  not not_73 (not_73_out, OP3);
  not not_74 (not_74_out, OP4);
  not not_75 (not_75_out, OP5);
  not not_76 (not_76_out, F0);
  not not_77 (not_77_out, F2);
  not not_78 (not_78_out, F4);
  not not_79 (not_79_out, OP0);
  not not_80 (not_80_out, OP1);
  not not_81 (not_81_out, OP2);
  not not_82 (not_82_out, OP3);
  not not_83 (not_83_out, OP4);
  not not_84 (not_84_out, OP5);
  not not_85 (not_85_out, F3);
  not not_86 (not_86_out, F4);
  not not_87 (not_87_out, OP0);
  not not_88 (not_88_out, OP1);
  not not_89 (not_89_out, OP4);
  not not_90 (not_90_out, OP5);
  not not_91 (not_91_out, OP0);
  not not_92 (not_92_out, OP2);
  not not_93 (not_93_out, OP4);
  not not_94 (not_94_out, OP5);
  not not_95 (not_95_out, OP0);
  not not_96 (not_96_out, OP1);
  not not_97 (not_97_out, OP2);
  not not_98 (not_98_out, OP4);
  not not_99 (not_99_out, OP5);
  not not_100 (not_100_out, F0);
  not not_101 (not_101_out, F1);
  not not_102 (not_102_out, F3);
  not not_103 (not_103_out, F4);
  not not_104 (not_104_out, OP0);
  not not_105 (not_105_out, OP1);
  not not_106 (not_106_out, OP2);
  not not_107 (not_107_out, OP4);
  not not_108 (not_108_out, OP5);
  not not_109 (not_109_out, F0);
  not not_110 (not_110_out, F2);
  not not_111 (not_111_out, F3);
  not not_112 (not_112_out, F4);
  not not_113 (not_113_out, OP0);
  not not_114 (not_114_out, OP1);
  not not_115 (not_115_out, OP2);
  not not_116 (not_116_out, OP4);
  not not_117 (not_117_out, OP5);
  not not_118 (not_118_out, F1);
  not not_119 (not_119_out, F2);
  not not_120 (not_120_out, F3);
  not not_121 (not_121_out, F4);
  not not_122 (not_122_out, OP0);
  not not_123 (not_123_out, OP1);
  not not_124 (not_124_out, OP2);
  not not_125 (not_125_out, OP4);
  not not_126 (not_126_out, OP5);
  not not_127 (not_127_out, F2);
  not not_128 (not_128_out, F4);
  not not_129 (not_129_out, OP0);
  not not_130 (not_130_out, OP1);
  not not_131 (not_131_out, OP4);
  not not_132 (not_132_out, OP5);
  not not_133 (not_133_out, OP1);
  not not_134 (not_134_out, OP2);
  not not_135 (not_135_out, OP4);
  not not_136 (not_136_out, OP5);
  not not_137 (not_137_out, OP2);
  not not_138 (not_138_out, OP4);
  not not_139 (not_139_out, OP0);
  not not_140 (not_140_out, OP1);
  not not_141 (not_141_out, OP2);
  not not_142 (not_142_out, OP3);
  not not_143 (not_143_out, OP4);
  not not_144 (not_144_out, OP5);
  not not_145 (not_145_out, F2);
  not not_146 (not_146_out, F4);
  not not_147 (not_147_out, OP0);
  not not_148 (not_148_out, OP1);
  not not_149 (not_149_out, OP2);
  not not_150 (not_150_out, OP3);
  not not_151 (not_151_out, OP4);
  not not_152 (not_152_out, OP5);
  not not_153 (not_153_out, F3);
  not not_154 (not_154_out, F4);
  not not_155 (not_155_out, OP0);
  not not_156 (not_156_out, OP2);
  not not_157 (not_157_out, OP4);
  not not_158 (not_158_out, OP5);
  not not_159 (not_159_out, OP1);
  not not_160 (not_160_out, OP4);
  not not_161 (not_161_out, OP5);
  and and_1 (and_1_out, not_1_out, not_2_out, not_3_out, not_4_out, not_5_out, not_6_out, not_7_out, not_8_out, not_9_out, F5);
  and and_2 (and_2_out, not_10_out, not_11_out, not_12_out, not_13_out, not_14_out, not_15_out, not_16_out, not_17_out, not_18_out, F5);
  and and_3 (and_3_out, not_19_out, not_20_out, not_21_out, not_22_out, not_23_out, not_24_out, F1, not_25_out, F3, not_26_out, F5);
  and and_4 (and_4_out, not_27_out, not_28_out, not_29_out, not_30_out, not_31_out, F0, F1, not_32_out, not_33_out, not_34_out, not_35_out);
  and and_5 (and_5_out, not_36_out, not_37_out, OP3, not_38_out, not_39_out);
  and and_6 (and_6_out, not_40_out, not_41_out, OP3, not_42_out, not_43_out);
  and and_7 (and_7_out, not_44_out, not_45_out, OP3, not_46_out, not_47_out);
  and and_8 (and_8_out, OP0, OP1, not_48_out, not_49_out, OP5);
  and and_9 (and_9_out, not_50_out, not_51_out, not_52_out, not_53_out, not_54_out, not_55_out, not_56_out, not_57_out, F2, not_58_out, not_59_out, F5);
  and and_10 (and_10_out, not_60_out, not_61_out, not_62_out, not_63_out, not_64_out, not_65_out, not_66_out, F1, not_67_out, not_68_out, not_69_out);
  and and_11 (and_11_out, not_70_out, not_71_out, not_72_out, not_73_out, not_74_out, not_75_out, not_76_out, F1, not_77_out, not_78_out, F5);
  and and_12 (and_12_out, not_79_out, not_80_out, not_81_out, not_82_out, not_83_out, not_84_out, F0, F1, F2, not_85_out, not_86_out, F5);
  and and_13 (and_13_out, not_87_out, not_88_out, OP2, OP3, not_89_out, not_90_out);
  and and_14 (and_14_out, not_91_out, OP1, not_92_out, OP3, not_93_out, not_94_out);
  and and_15 (and_15_out, not_95_out, not_96_out, not_97_out, not_98_out, not_99_out, not_100_out, not_101_out, not_102_out, not_103_out, F5);
  and and_16 (and_16_out, not_104_out, not_105_out, not_106_out, not_107_out, not_108_out, not_109_out, not_110_out, not_111_out, not_112_out, F5);
  and and_17 (and_17_out, not_113_out, not_114_out, not_115_out, not_116_out, not_117_out, not_118_out, not_119_out, not_120_out, not_121_out, F5);
  and and_18 (and_18_out, not_122_out, not_123_out, not_124_out, not_125_out, not_126_out, F0, F1, not_127_out, F3, not_128_out, F5);
  and and_19 (and_19_out, not_129_out, not_130_out, OP3, not_131_out, not_132_out);
  and and_20 (and_20_out, not_133_out, not_134_out, OP3, not_135_out, not_136_out);
  and and_21 (and_21_out, OP0, OP1, not_137_out, not_138_out, OP5);
  and and_22 (and_22_out, not_139_out, not_140_out, not_141_out, not_142_out, not_143_out, not_144_out, F1, not_145_out, F3, not_146_out, F5);
  and and_23 (and_23_out, not_147_out, not_148_out, not_149_out, not_150_out, not_151_out, not_152_out, F0, F2, not_153_out, not_154_out, F5);
  and and_24 (and_24_out, not_155_out, OP1, not_156_out, OP3, not_157_out, not_158_out);
  and and_25 (and_25_out, OP0, not_159_out, OP2, OP3, not_160_out, not_161_out);
  or or_1 (S0, and_1_out, and_2_out, and_3_out, and_4_out, and_5_out, and_6_out, and_7_out, and_8_out);
  or or_2 (S1, and_9_out, and_10_out, and_11_out, and_12_out, and_13_out, and_14_out);
  or or_3 (S2, and_15_out, and_16_out, and_17_out, and_18_out, and_19_out, and_20_out, and_21_out);
  or or_4 (S3, and_22_out, and_23_out, and_24_out, and_25_out);
endmodule

// 控制信号生成
module \控制信号自动生成  (
  input  OP0,
  input  OP1,
  input  OP2,
  input  OP3,
  input  OP4,
  input  OP5,
  input  F0,
  input  F1,
  input  F2,
  input  F3,
  input  F4,
  input  F5,
  output MemToReg,
  output MemWrite,
  output ALU_SRC,
  output RegWrite,
  output SysCALL,
  output SignedExt,
  output RegDst,
  output BEQ,
  output BNE,
  output JR,
  output JUMP,
  output JAL
);

  wire and_3_out, and_4_out, and_5_out, and_6_out, and_7_out, and_8_out, and_9_out, and_10_out, and_11_out,
       and_12_out, and_13_out, and_14_out, and_15_out, and_16_out, and_17_out, and_18_out, and_19_out,
       and_20_out, and_21_out, and_22_out, and_23_out, and_24_out, and_25_out, and_26_out, and_27_out,
       and_29_out, and_30_out, and_31_out, and_32_out, and_33_out, and_34_out, and_35_out, and_36_out,
       and_37_out, and_38_out, and_39_out, and_40_out, and_41_out, and_42_out, and_43_out, and_44_out,
       and_45_out, and_49_out, and_50_out, and_51_out, not_1_out, not_2_out, not_3_out, not_4_out, not_5_out,
       not_6_out, not_7_out, not_8_out, not_9_out, not_10_out, not_11_out, not_12_out, not_13_out,
       not_14_out, not_15_out, not_16_out, not_17_out, not_18_out, not_19_out, not_20_out, not_21_out,
       not_22_out, not_23_out, not_24_out, not_25_out, not_26_out, not_27_out, not_28_out, not_29_out,
       not_30_out, not_31_out, not_32_out, not_33_out, not_34_out, not_35_out, not_36_out, not_37_out,
       not_38_out, not_39_out, not_40_out, not_41_out, not_42_out, not_43_out, not_44_out, not_45_out,
       not_46_out, not_47_out, not_48_out, not_49_out, not_50_out, not_51_out, not_52_out, not_53_out,
       not_54_out, not_55_out, not_56_out, not_57_out, not_58_out, not_59_out, not_60_out, not_61_out,
       not_62_out, not_63_out, not_64_out, not_65_out, not_66_out, not_67_out, not_68_out, not_69_out,
       not_70_out, not_71_out, not_72_out, not_73_out, not_74_out, not_75_out, not_76_out, not_77_out,
       not_78_out, not_79_out, not_80_out, not_81_out, not_82_out, not_83_out, not_84_out, not_85_out,
       not_86_out, not_87_out, not_88_out, not_89_out, not_90_out, not_91_out, not_92_out, not_93_out,
       not_94_out, not_95_out, not_96_out, not_97_out, not_98_out, not_99_out, not_100_out, not_101_out,
       not_102_out, not_103_out, not_104_out, not_105_out, not_106_out, not_107_out, not_108_out,
       not_109_out, not_110_out, not_111_out, not_112_out, not_113_out, not_114_out, not_115_out,
       not_116_out, not_117_out, not_118_out, not_119_out, not_120_out, not_121_out, not_122_out,
       not_123_out, not_124_out, not_125_out, not_126_out, not_127_out, not_128_out, not_129_out,
       not_130_out, not_131_out, not_132_out, not_133_out, not_134_out, not_135_out, not_136_out,
       not_137_out, not_138_out, not_139_out, not_140_out, not_141_out, not_142_out, not_143_out,
       not_144_out, not_145_out, not_146_out, not_147_out, not_148_out, not_149_out, not_150_out,
       not_151_out, not_152_out, not_153_out, not_154_out, not_155_out, not_156_out, not_157_out,
       not_158_out, not_159_out, not_160_out, not_161_out, not_162_out, not_163_out, not_164_out,
       not_165_out, not_166_out, not_167_out, not_168_out, not_169_out, not_170_out, not_171_out,
       not_172_out, not_173_out, not_174_out, not_175_out, not_176_out, not_177_out, not_178_out,
       not_179_out, not_180_out, not_181_out, not_182_out, not_183_out, not_184_out, not_185_out,
       not_186_out, not_187_out, not_188_out, not_189_out, not_190_out, not_191_out, not_192_out,
       not_193_out, not_194_out, not_195_out, not_196_out, not_197_out, not_198_out, not_199_out,
       not_200_out, not_201_out, not_202_out, not_203_out, not_204_out, not_205_out, not_206_out,
       not_207_out, not_208_out, not_209_out, not_210_out, not_211_out, not_212_out, not_213_out,
       not_214_out, not_215_out, not_216_out, not_217_out, not_218_out, not_219_out, not_220_out,
       not_221_out, not_222_out, not_223_out, not_224_out, not_225_out, not_226_out, not_227_out,
       not_228_out, not_229_out, not_230_out, not_231_out, not_232_out, not_233_out, not_234_out,
       not_235_out, not_236_out, not_237_out, not_238_out, not_239_out, not_240_out, not_241_out,
       not_242_out, not_243_out, not_244_out, not_245_out, not_246_out, not_247_out, not_248_out,
       not_249_out, not_250_out, not_251_out, not_252_out, not_253_out, not_254_out, not_255_out,
       not_256_out, not_257_out, not_258_out, not_259_out, not_260_out, not_261_out, not_262_out,
       not_263_out, not_264_out, not_265_out, not_266_out, not_267_out, not_268_out, not_269_out,
       not_270_out, not_271_out, not_272_out, not_273_out, not_274_out, not_275_out, not_276_out,
       not_277_out, not_278_out, not_279_out, not_280_out, not_281_out, not_282_out, not_283_out,
       not_284_out, not_285_out, not_286_out, not_287_out, not_288_out, not_289_out, not_290_out,
       not_291_out, not_292_out, not_293_out, not_294_out, not_295_out, not_296_out, not_297_out,
       not_298_out, not_299_out, not_300_out, not_301_out, not_302_out, not_303_out, not_304_out,
       not_305_out, not_306_out, not_307_out, not_308_out, not_309_out, not_310_out, not_311_out,
       not_312_out, not_313_out, not_314_out, not_315_out, not_316_out, not_317_out, not_318_out,
       not_319_out, not_320_out, not_321_out, not_322_out, not_323_out, not_324_out, not_325_out,
       not_326_out, not_327_out, not_328_out, not_329_out, not_330_out, not_331_out, not_332_out,
       not_333_out, not_334_out, not_335_out, not_336_out, not_337_out, not_338_out, not_339_out,
       not_340_out, not_341_out, not_342_out, not_343_out, not_344_out, not_345_out, not_346_out,
       not_347_out, not_348_out, not_349_out, not_350_out, not_351_out, not_352_out, not_353_out,
       not_354_out, not_355_out, not_356_out;

  not not_1 (not_1_out, OP4);
  not not_2 (not_2_out, OP3);
  not not_3 (not_3_out, OP2);
  not not_4 (not_4_out, OP4);
  not not_5 (not_5_out, OP2);
  not not_6 (not_6_out, OP5);
  not not_7 (not_7_out, OP4);
  not not_8 (not_8_out, OP2);
  not not_9 (not_9_out, OP1);
  not not_10 (not_10_out, OP0);
  not not_11 (not_11_out, OP5);
  not not_12 (not_12_out, OP4);
  not not_13 (not_13_out, OP1);
  not not_14 (not_14_out, OP0);
  not not_15 (not_15_out, OP5);
  not not_16 (not_16_out, OP4);
  not not_17 (not_17_out, OP2);
  not not_18 (not_18_out, OP1);
  not not_19 (not_19_out, OP5);
  not not_20 (not_20_out, OP4);
  not not_21 (not_21_out, OP2);
  not not_22 (not_22_out, OP0);
  not not_23 (not_23_out, OP5);
  not not_24 (not_24_out, OP4);
  not not_25 (not_25_out, OP1);
  not not_26 (not_26_out, OP4);
  not not_27 (not_27_out, OP3);
  not not_28 (not_28_out, OP2);
  not not_29 (not_29_out, OP4);
  not not_30 (not_30_out, OP2);
  not not_31 (not_31_out, OP5);
  not not_32 (not_32_out, OP4);
  not not_33 (not_33_out, OP3);
  not not_34 (not_34_out, OP2);
  not not_35 (not_35_out, OP1);
  not not_36 (not_36_out, OP0);
  not not_37 (not_37_out, F5);
  not not_38 (not_38_out, F4);
  not not_39 (not_39_out, F3);
  not not_40 (not_40_out, F2);
  not not_41 (not_41_out, F1);
  not not_42 (not_42_out, F0);
  not not_43 (not_43_out, OP5);
  not not_44 (not_44_out, OP4);
  not not_45 (not_45_out, OP3);
  not not_46 (not_46_out, OP2);
  not not_47 (not_47_out, OP1);
  not not_48 (not_48_out, OP0);
  not not_49 (not_49_out, F5);
  not not_50 (not_50_out, F4);
  not not_51 (not_51_out, F3);
  not not_52 (not_52_out, F2);
  not not_53 (not_53_out, OP5);
  not not_54 (not_54_out, OP4);
  not not_55 (not_55_out, OP3);
  not not_56 (not_56_out, OP2);
  not not_57 (not_57_out, OP1);
  not not_58 (not_58_out, OP0);
  not not_59 (not_59_out, F5);
  not not_60 (not_60_out, F4);
  not not_61 (not_61_out, F3);
  not not_62 (not_62_out, F2);
  not not_63 (not_63_out, F0);
  not not_64 (not_64_out, OP5);
  not not_65 (not_65_out, OP4);
  not not_66 (not_66_out, OP3);
  not not_67 (not_67_out, OP2);
  not not_68 (not_68_out, OP1);
  not not_69 (not_69_out, OP0);
  not not_70 (not_70_out, F4);
  not not_71 (not_71_out, F3);
  not not_72 (not_72_out, F2);
  not not_73 (not_73_out, F1);
  not not_74 (not_74_out, F0);
  not not_75 (not_75_out, OP5);
  not not_76 (not_76_out, OP4);
  not not_77 (not_77_out, OP3);
  not not_78 (not_78_out, OP2);
  not not_79 (not_79_out, OP1);
  not not_80 (not_80_out, OP0);
  not not_81 (not_81_out, F4);
  not not_82 (not_82_out, F3);
  not not_83 (not_83_out, F2);
  not not_84 (not_84_out, F1);
  not not_85 (not_85_out, OP5);
  not not_86 (not_86_out, OP4);
  not not_87 (not_87_out, OP3);
  not not_88 (not_88_out, OP2);
  not not_89 (not_89_out, OP1);
  not not_90 (not_90_out, OP0);
  not not_91 (not_91_out, F4);
  not not_92 (not_92_out, F3);
  not not_93 (not_93_out, F2);
  not not_94 (not_94_out, F0);
  not not_95 (not_95_out, OP5);
  not not_96 (not_96_out, OP4);
  not not_97 (not_97_out, OP3);
  not not_98 (not_98_out, OP2);
  not not_99 (not_99_out, OP1);
  not not_100 (not_100_out, OP0);
  not not_101 (not_101_out, F4);
  not not_102 (not_102_out, F3);
  not not_103 (not_103_out, F1);
  not not_104 (not_104_out, F0);
  not not_105 (not_105_out, OP5);
  not not_106 (not_106_out, OP4);
  not not_107 (not_107_out, OP3);
  not not_108 (not_108_out, OP2);
  not not_109 (not_109_out, OP1);
  not not_110 (not_110_out, OP0);
  not not_111 (not_111_out, F4);
  not not_112 (not_112_out, F3);
  not not_113 (not_113_out, F1);
  not not_114 (not_114_out, OP5);
  not not_115 (not_115_out, OP4);
  not not_116 (not_116_out, OP3);
  not not_117 (not_117_out, OP2);
  not not_118 (not_118_out, OP1);
  not not_119 (not_119_out, OP0);
  not not_120 (not_120_out, F4);
  not not_121 (not_121_out, F3);
  not not_122 (not_122_out, OP5);
  not not_123 (not_123_out, OP4);
  not not_124 (not_124_out, OP3);
  not not_125 (not_125_out, OP2);
  not not_126 (not_126_out, OP1);
  not not_127 (not_127_out, OP0);
  not not_128 (not_128_out, F4);
  not not_129 (not_129_out, F2);
  not not_130 (not_130_out, F0);
  not not_131 (not_131_out, OP5);
  not not_132 (not_132_out, OP4);
  not not_133 (not_133_out, OP3);
  not not_134 (not_134_out, OP2);
  not not_135 (not_135_out, OP1);
  not not_136 (not_136_out, OP0);
  not not_137 (not_137_out, F4);
  not not_138 (not_138_out, F2);
  not not_139 (not_139_out, OP5);
  not not_140 (not_140_out, OP4);
  not not_141 (not_141_out, OP3);
  not not_142 (not_142_out, OP2);
  not not_143 (not_143_out, OP5);
  not not_144 (not_144_out, OP4);
  not not_145 (not_145_out, OP2);
  not not_146 (not_146_out, OP1);
  not not_147 (not_147_out, OP0);
  not not_148 (not_148_out, OP5);
  not not_149 (not_149_out, OP4);
  not not_150 (not_150_out, OP1);
  not not_151 (not_151_out, OP0);
  not not_152 (not_152_out, OP5);
  not not_153 (not_153_out, OP4);
  not not_154 (not_154_out, OP2);
  not not_155 (not_155_out, OP1);
  not not_156 (not_156_out, OP5);
  not not_157 (not_157_out, OP4);
  not not_158 (not_158_out, OP2);
  not not_159 (not_159_out, OP0);
  not not_160 (not_160_out, OP5);
  not not_161 (not_161_out, OP4);
  not not_162 (not_162_out, OP1);
  not not_163 (not_163_out, OP4);
  not not_164 (not_164_out, OP3);
  not not_165 (not_165_out, OP2);
  not not_166 (not_166_out, OP5);
  not not_167 (not_167_out, OP4);
  not not_168 (not_168_out, OP3);
  not not_169 (not_169_out, OP2);
  not not_170 (not_170_out, OP1);
  not not_171 (not_171_out, OP0);
  not not_172 (not_172_out, F5);
  not not_173 (not_173_out, F4);
  not not_174 (not_174_out, F1);
  not not_175 (not_175_out, F0);
  not not_176 (not_176_out, OP5);
  not not_177 (not_177_out, OP4);
  not not_178 (not_178_out, OP2);
  not not_179 (not_179_out, OP1);
  not not_180 (not_180_out, OP0);
  not not_181 (not_181_out, OP5);
  not not_182 (not_182_out, OP4);
  not not_183 (not_183_out, OP2);
  not not_184 (not_184_out, OP1);
  not not_185 (not_185_out, OP5);
  not not_186 (not_186_out, OP4);
  not not_187 (not_187_out, OP2);
  not not_188 (not_188_out, OP0);
  not not_189 (not_189_out, OP4);
  not not_190 (not_190_out, OP3);
  not not_191 (not_191_out, OP2);
  not not_192 (not_192_out, OP4);
  not not_193 (not_193_out, OP2);
  not not_194 (not_194_out, OP5);
  not not_195 (not_195_out, OP4);
  not not_196 (not_196_out, OP3);
  not not_197 (not_197_out, OP2);
  not not_198 (not_198_out, OP1);
  not not_199 (not_199_out, OP0);
  not not_200 (not_200_out, F5);
  not not_201 (not_201_out, F4);
  not not_202 (not_202_out, F3);
  not not_203 (not_203_out, F2);
  not not_204 (not_204_out, F1);
  not not_205 (not_205_out, F0);
  not not_206 (not_206_out, OP5);
  not not_207 (not_207_out, OP4);
  not not_208 (not_208_out, OP3);
  not not_209 (not_209_out, OP2);
  not not_210 (not_210_out, OP1);
  not not_211 (not_211_out, OP0);
  not not_212 (not_212_out, F5);
  not not_213 (not_213_out, F4);
  not not_214 (not_214_out, F3);
  not not_215 (not_215_out, F2);
  not not_216 (not_216_out, OP5);
  not not_217 (not_217_out, OP4);
  not not_218 (not_218_out, OP3);
  not not_219 (not_219_out, OP2);
  not not_220 (not_220_out, OP1);
  not not_221 (not_221_out, OP0);
  not not_222 (not_222_out, F5);
  not not_223 (not_223_out, F4);
  not not_224 (not_224_out, F3);
  not not_225 (not_225_out, F2);
  not not_226 (not_226_out, F0);
  not not_227 (not_227_out, OP5);
  not not_228 (not_228_out, OP4);
  not not_229 (not_229_out, OP3);
  not not_230 (not_230_out, OP2);
  not not_231 (not_231_out, OP1);
  not not_232 (not_232_out, OP0);
  not not_233 (not_233_out, F4);
  not not_234 (not_234_out, F3);
  not not_235 (not_235_out, F2);
  not not_236 (not_236_out, F1);
  not not_237 (not_237_out, F0);
  not not_238 (not_238_out, OP5);
  not not_239 (not_239_out, OP4);
  not not_240 (not_240_out, OP3);
  not not_241 (not_241_out, OP2);
  not not_242 (not_242_out, OP1);
  not not_243 (not_243_out, OP0);
  not not_244 (not_244_out, F4);
  not not_245 (not_245_out, F3);
  not not_246 (not_246_out, F2);
  not not_247 (not_247_out, F1);
  not not_248 (not_248_out, OP5);
  not not_249 (not_249_out, OP4);
  not not_250 (not_250_out, OP3);
  not not_251 (not_251_out, OP2);
  not not_252 (not_252_out, OP1);
  not not_253 (not_253_out, OP0);
  not not_254 (not_254_out, F4);
  not not_255 (not_255_out, F3);
  not not_256 (not_256_out, F2);
  not not_257 (not_257_out, F0);
  not not_258 (not_258_out, OP5);
  not not_259 (not_259_out, OP4);
  not not_260 (not_260_out, OP3);
  not not_261 (not_261_out, OP2);
  not not_262 (not_262_out, OP1);
  not not_263 (not_263_out, OP0);
  not not_264 (not_264_out, F4);
  not not_265 (not_265_out, F3);
  not not_266 (not_266_out, F1);
  not not_267 (not_267_out, F0);
  not not_268 (not_268_out, OP5);
  not not_269 (not_269_out, OP4);
  not not_270 (not_270_out, OP3);
  not not_271 (not_271_out, OP2);
  not not_272 (not_272_out, OP1);
  not not_273 (not_273_out, OP0);
  not not_274 (not_274_out, F4);
  not not_275 (not_275_out, F3);
  not not_276 (not_276_out, F1);
  not not_277 (not_277_out, OP5);
  not not_278 (not_278_out, OP4);
  not not_279 (not_279_out, OP3);
  not not_280 (not_280_out, OP2);
  not not_281 (not_281_out, OP1);
  not not_282 (not_282_out, OP0);
  not not_283 (not_283_out, F4);
  not not_284 (not_284_out, F3);
  not not_285 (not_285_out, OP5);
  not not_286 (not_286_out, OP4);
  not not_287 (not_287_out, OP3);
  not not_288 (not_288_out, OP2);
  not not_289 (not_289_out, OP1);
  not not_290 (not_290_out, OP0);
  not not_291 (not_291_out, F4);
  not not_292 (not_292_out, F2);
  not not_293 (not_293_out, F0);
  not not_294 (not_294_out, OP5);
  not not_295 (not_295_out, OP4);
  not not_296 (not_296_out, OP3);
  not not_297 (not_297_out, OP2);
  not not_298 (not_298_out, OP1);
  not not_299 (not_299_out, OP0);
  not not_300 (not_300_out, F4);
  not not_301 (not_301_out, F2);
  not not_302 (not_302_out, OP5);
  not not_303 (not_303_out, OP4);
  not not_304 (not_304_out, OP3);
  not not_305 (not_305_out, OP2);
  not not_306 (not_306_out, OP1);
  not not_307 (not_307_out, OP0);
  not not_308 (not_308_out, F5);
  not not_309 (not_309_out, F4);
  not not_310 (not_310_out, F2);
  not not_311 (not_311_out, F1);
  not not_312 (not_312_out, F0);
  not not_313 (not_313_out, OP5);
  not not_314 (not_314_out, OP4);
  not not_315 (not_315_out, OP3);
  not not_316 (not_316_out, OP1);
  not not_317 (not_317_out, OP0);
  not not_318 (not_318_out, OP5);
  not not_319 (not_319_out, OP4);
  not not_320 (not_320_out, OP3);
  not not_321 (not_321_out, OP1);
  not not_322 (not_322_out, OP5);
  not not_323 (not_323_out, OP4);
  not not_324 (not_324_out, OP3);
  not not_325 (not_325_out, OP2);
  not not_326 (not_326_out, OP1);
  not not_327 (not_327_out, OP0);
  not not_328 (not_328_out, F5);
  not not_329 (not_329_out, F4);
  not not_330 (not_330_out, F2);
  not not_331 (not_331_out, F1);
  not not_332 (not_332_out, F0);
  not not_333 (not_333_out, OP5);
  not not_334 (not_334_out, OP4);
  not not_335 (not_335_out, OP3);
  not not_336 (not_336_out, OP2);
  not not_337 (not_337_out, OP1);
  not not_338 (not_338_out, OP0);
  not not_339 (not_339_out, F5);
  not not_340 (not_340_out, F4);
  not not_341 (not_341_out, F2);
  not not_342 (not_342_out, F1);
  not not_343 (not_343_out, F0);
  not not_344 (not_344_out, OP5);
  not not_345 (not_345_out, OP4);
  not not_346 (not_346_out, OP3);
  not not_347 (not_347_out, OP2);
  not not_348 (not_348_out, OP0);
  not not_349 (not_349_out, OP5);
  not not_350 (not_350_out, OP4);
  not not_351 (not_351_out, OP3);
  not not_352 (not_352_out, OP2);
  not not_353 (not_353_out, OP5);
  not not_354 (not_354_out, OP4);
  not not_355 (not_355_out, OP3);
  not not_356 (not_356_out, OP2);
  and and_1 (MemToReg, OP5, not_1_out, not_2_out, not_3_out, OP1, OP0);
  and and_2 (MemWrite, OP5, not_4_out, OP3, not_5_out, OP1, OP0);
  and and_3 (and_3_out, not_6_out, not_7_out, OP3, not_8_out, not_9_out, not_10_out);
  and and_4 (and_4_out, not_11_out, not_12_out, OP3, OP2, not_13_out, not_14_out);
  and and_5 (and_5_out, not_15_out, not_16_out, OP3, not_17_out, not_18_out, OP0);
  and and_6 (and_6_out, not_19_out, not_20_out, OP3, not_21_out, OP1, not_22_out);
  and and_7 (and_7_out, not_23_out, not_24_out, OP3, OP2, not_25_out, OP0);
  and and_8 (and_8_out, OP5, not_26_out, not_27_out, not_28_out, OP1, OP0);
  and and_9 (and_9_out, OP5, not_29_out, OP3, not_30_out, OP1, OP0);
  and and_10 (and_10_out, not_31_out, not_32_out, not_33_out, not_34_out, not_35_out, not_36_out, not_37_out, not_38_out, not_39_out, not_40_out, not_41_out, not_42_out);
  and and_11 (and_11_out, not_43_out, not_44_out, not_45_out, not_46_out, not_47_out, not_48_out, not_49_out, not_50_out, not_51_out, not_52_out, F1, F0);
  and and_12 (and_12_out, not_53_out, not_54_out, not_55_out, not_56_out, not_57_out, not_58_out, not_59_out, not_60_out, not_61_out, not_62_out, F1, not_63_out);
  and and_13 (and_13_out, not_64_out, not_65_out, not_66_out, not_67_out, not_68_out, not_69_out, F5, not_70_out, not_71_out, not_72_out, not_73_out, not_74_out);
  and and_14 (and_14_out, not_75_out, not_76_out, not_77_out, not_78_out, not_79_out, not_80_out, F5, not_81_out, not_82_out, not_83_out, not_84_out, F0);
  and and_15 (and_15_out, not_85_out, not_86_out, not_87_out, not_88_out, not_89_out, not_90_out, F5, not_91_out, not_92_out, not_93_out, F1, not_94_out);
  and and_16 (and_16_out, not_95_out, not_96_out, not_97_out, not_98_out, not_99_out, not_100_out, F5, not_101_out, not_102_out, F2, not_103_out, not_104_out);
  and and_17 (and_17_out, not_105_out, not_106_out, not_107_out, not_108_out, not_109_out, not_110_out, F5, not_111_out, not_112_out, F2, not_113_out, F0);
  and and_18 (and_18_out, not_114_out, not_115_out, not_116_out, not_117_out, not_118_out, not_119_out, F5, not_120_out, not_121_out, F2, F1, F0);
  and and_19 (and_19_out, not_122_out, not_123_out, not_124_out, not_125_out, not_126_out, not_127_out, F5, not_128_out, F3, not_129_out, F1, not_130_out);
  and and_20 (and_20_out, not_131_out, not_132_out, not_133_out, not_134_out, not_135_out, not_136_out, F5, not_137_out, F3, not_138_out, F1, F0);
  and and_21 (and_21_out, not_139_out, not_140_out, not_141_out, not_142_out, OP1, OP0);
  and and_22 (and_22_out, not_143_out, not_144_out, OP3, not_145_out, not_146_out, not_147_out);
  and and_23 (and_23_out, not_148_out, not_149_out, OP3, OP2, not_150_out, not_151_out);
  and and_24 (and_24_out, not_152_out, not_153_out, OP3, not_154_out, not_155_out, OP0);
  and and_25 (and_25_out, not_156_out, not_157_out, OP3, not_158_out, OP1, not_159_out);
  and and_26 (and_26_out, not_160_out, not_161_out, OP3, OP2, not_162_out, OP0);
  and and_27 (and_27_out, OP5, not_163_out, not_164_out, not_165_out, OP1, OP0);
  and and_28 (SysCALL, not_166_out, not_167_out, not_168_out, not_169_out, not_170_out, not_171_out, not_172_out, not_173_out, F3, F2, not_174_out, not_175_out);
  and and_29 (and_29_out, not_176_out, not_177_out, OP3, not_178_out, not_179_out, not_180_out);
  and and_30 (and_30_out, not_181_out, not_182_out, OP3, not_183_out, not_184_out, OP0);
  and and_31 (and_31_out, not_185_out, not_186_out, OP3, not_187_out, OP1, not_188_out);
  and and_32 (and_32_out, OP5, not_189_out, not_190_out, not_191_out, OP1, OP0);
  and and_33 (and_33_out, OP5, not_192_out, OP3, not_193_out, OP1, OP0);
  and and_34 (and_34_out, not_194_out, not_195_out, not_196_out, not_197_out, not_198_out, not_199_out, not_200_out, not_201_out, not_202_out, not_203_out, not_204_out, not_205_out);
  and and_35 (and_35_out, not_206_out, not_207_out, not_208_out, not_209_out, not_210_out, not_211_out, not_212_out, not_213_out, not_214_out, not_215_out, F1, F0);
  and and_36 (and_36_out, not_216_out, not_217_out, not_218_out, not_219_out, not_220_out, not_221_out, not_222_out, not_223_out, not_224_out, not_225_out, F1, not_226_out);
  and and_37 (and_37_out, not_227_out, not_228_out, not_229_out, not_230_out, not_231_out, not_232_out, F5, not_233_out, not_234_out, not_235_out, not_236_out, not_237_out);
  and and_38 (and_38_out, not_238_out, not_239_out, not_240_out, not_241_out, not_242_out, not_243_out, F5, not_244_out, not_245_out, not_246_out, not_247_out, F0);
  and and_39 (and_39_out, not_248_out, not_249_out, not_250_out, not_251_out, not_252_out, not_253_out, F5, not_254_out, not_255_out, not_256_out, F1, not_257_out);
  and and_40 (and_40_out, not_258_out, not_259_out, not_260_out, not_261_out, not_262_out, not_263_out, F5, not_264_out, not_265_out, F2, not_266_out, not_267_out);
  and and_41 (and_41_out, not_268_out, not_269_out, not_270_out, not_271_out, not_272_out, not_273_out, F5, not_274_out, not_275_out, F2, not_276_out, F0);
  and and_42 (and_42_out, not_277_out, not_278_out, not_279_out, not_280_out, not_281_out, not_282_out, F5, not_283_out, not_284_out, F2, F1, F0);
  and and_43 (and_43_out, not_285_out, not_286_out, not_287_out, not_288_out, not_289_out, not_290_out, F5, not_291_out, F3, not_292_out, F1, not_293_out);
  and and_44 (and_44_out, not_294_out, not_295_out, not_296_out, not_297_out, not_298_out, not_299_out, F5, not_300_out, F3, not_301_out, F1, F0);
  and and_45 (and_45_out, not_302_out, not_303_out, not_304_out, not_305_out, not_306_out, not_307_out, not_308_out, not_309_out, F3, not_310_out, not_311_out, not_312_out);
  and and_46 (BEQ, not_313_out, not_314_out, not_315_out, OP2, not_316_out, not_317_out);
  and and_47 (BNE, not_318_out, not_319_out, not_320_out, OP2, not_321_out, OP0);
  and and_48 (JR, not_322_out, not_323_out, not_324_out, not_325_out, not_326_out, not_327_out, not_328_out, not_329_out, F3, not_330_out, not_331_out, not_332_out);
  and and_49 (and_49_out, not_333_out, not_334_out, not_335_out, not_336_out, not_337_out, not_338_out, not_339_out, not_340_out, F3, not_341_out, not_342_out, not_343_out);
  and and_50 (and_50_out, not_344_out, not_345_out, not_346_out, not_347_out, OP1, not_348_out);
  and and_51 (and_51_out, not_349_out, not_350_out, not_351_out, not_352_out, OP1, OP0);
  and and_52 (JAL, not_353_out, not_354_out, not_355_out, not_356_out, OP1, OP0);
  or or_1 (ALU_SRC, and_3_out, and_4_out, and_5_out, and_6_out, and_7_out, and_8_out, and_9_out);
  or or_2 (SignedExt, and_29_out, and_30_out, and_31_out, and_32_out, and_33_out);
  or or_3 (JUMP, and_49_out, and_50_out, and_51_out);
  or or_4 (RegWrite, and_10_out, and_11_out, and_12_out, and_13_out, and_14_out, and_15_out, and_16_out, and_17_out, and_18_out, and_19_out, and_20_out, and_21_out, and_22_out, and_23_out, and_24_out, and_25_out, and_26_out, and_27_out);
  or or_5 (RegDst, and_34_out, and_35_out, and_36_out, and_37_out, and_38_out, and_39_out, and_40_out, and_41_out, and_42_out, and_43_out, and_44_out, and_45_out);
endmodule

// ALU
module MIPS_ALU (
  input  [4:0] shamt,
  input  [31:0] X,
  input  [31:0] Y,
  input  [3:0] AluOP,
  output Equal,
  output [31:0] Result,
  output [31:0] Result_2
);

  wire [0:0] comparator_1_lt, comparator_2_lt;
  wire [31:0] adder_1_out, AND_out, divider_1_out, divider_1_rem, multiplier_1_cout, multiplier_1_out,
       NOR_out, OR_out, shifter_1_out, shifter_2_out, shifter_3_out, subtractor_1_out, XOR_out;

  assign AND_out = X & Y;  // AND_Gate AND, 32 bits wide
  assign OR_out = X | Y;  // OR_Gate OR, 32 bits wide
  Shifter #(.width(32)) shifter_1 (.in(Y), .\dist (shamt), .out(shifter_1_out));
  Shifter #(.width(32), .shift("ar")) shifter_2 (.in(Y), .\dist (shamt), .out(shifter_2_out));
  Shifter #(.width(32), .shift("lr")) shifter_3 (.in(Y), .\dist (shamt), .out(shifter_3_out));
  Multiplier #(.width(32)) multiplier_1 (.a(X), .b(Y), .out(multiplier_1_out), .cout(multiplier_1_cout));  // open: cin
  Divider #(.width(32)) divider_1 (.a(X), .b(Y), .out(divider_1_out), .rem(divider_1_rem));  // open: upper
  Adder #(.width(32)) adder_1 (.a(X), .b(Y), .out(adder_1_out));  // open: cin, cout
  Subtractor #(.width(32)) subtractor_1 (.a(X), .b(Y), .out(subtractor_1_out));  // open: bin, bout
  assign XOR_out = X ^ Y;  // XOR_Gate XOR, 32 bits wide
  assign NOR_out = ~(X | Y);  // NOR_Gate NOR, 32 bits wide
  Comparator #(.width(32)) comparator_1 (.a(X), .b(Y), .eq(Equal), .lt(comparator_1_lt[0]));  // open: gt
  Comparator #(.width(32), .mode("unsigned")) comparator_2 (.a(X), .b(Y), .lt(comparator_2_lt[0]));  // open: gt, eq
  Multiplexer #(.select(4), .width(32), .enable("false")) multiplexer_1 (
    .in0(shifter_1_out), .in1(shifter_2_out), .in2(shifter_3_out), .in3(multiplier_1_out),
    .in4(divider_1_out), .in5(adder_1_out), .in6(subtractor_1_out), .in7(AND_out), .in8(OR_out),
    .in9(XOR_out), .in10(NOR_out), .in11({{31{1'b0}}, comparator_1_lt[0]}),
    .in12({{31{1'b0}}, comparator_2_lt[0]}), .in13({32{1'b0}}), .in14({32{1'b0}}), .in15({32{1'b0}}),
    .out(Result), .sel(AluOP));
  Multiplexer #(.select(4), .width(32), .enable("false")) multiplexer_2 (
    .in0({32{1'b0}}), .in1({32{1'b0}}), .in2({32{1'b0}}), .in3(multiplier_1_cout), .in4(divider_1_rem),
    .in5({32{1'b0}}), .in6({32{1'b0}}), .in7({32{1'b0}}), .in8({32{1'b0}}), .in9({32{1'b0}}),
    .in10({32{1'b0}}), .in11({32{1'b0}}), .in12({32{1'b0}}), .in13({32{1'b0}}), .in14({32{1'b0}}),
    .in15({32{1'b0}}), .out(Result_2), .sel(AluOP));

  // Other names for the same wires on the sheet: Result2[31:0] = Result_2; S[3:0] = AluOP

  // Notes on the sheet:
  //   不要改变此引脚区域内容，也不要改变ALU封装形式
  //   输入引脚
  //   输出引脚
endmodule

module MIPS_Regifile (
  input  [31:0] Din,
  input  Clk,
  input  WE,
  input  [4:0] R1_num,
  input  [4:0] W_num,
  input  [4:0] R2_num,
  output [31:0] R1,
  output [31:0] R2
);

  // RegisterFile registerfile_1: pin names not known; wires that end beside it: Din, Clk, WE, W_num, R1_num, R2_num, R1, R2
endmodule

module \理想流水线  (
  output RegWrite,
  output MemWrite,
  output [31:0] IF_PC,
  output [31:0] ID_PC,
  output [31:0] EX_PC,
  output [31:0] M_PC,
  output [31:0] WB_PC,
  output [31:0] RDin,
  output [31:0] MDin,
  output [31:0] LedData
);

  wire AluSrcB, AluSrcB_ID_EX, and_1_out, and_2_out, Beq, Beq_ID_EX, Bne, Bne_ID_EX, Branch, CLK,
       clock_1_out, clock_2_out, comparator_1_eq, comparator_1_lt, d_ff_1_q, Equal, Go, IR1, IR2, IR3, Jal,
       Jal_EX_MEM, Jal_ID_EX, Jal_MEM_WB, Jmp, Jmp_ID_EX, Jr, Jr_ID_EX, MemToReg, MemToReg_EX_MEM,
       MemToReg_ID_EX, MemToReg_MEM_WB, MemWrite_EX_MEM, MemWrite_ID_EX, nand_1_out, RegDst, RegDst_EX_MEM,
       RegDst_ID_EX, RegDst_MEM_WB, RegWrite_EX_MEM, RegWrite_ID_EX, RegWrite_MEM_WB, RST, SignedExt,
       SignedExt_ID_EX, Syscall, W1, W2, W3;
  wire [3:0] AluOp, AluOp_ID_EX;
  wire [4:0] multiplexer_6_out, registerfile_1_p5, registerfile_1_p6, WriteReg, WriteReg_EX_MEM,
       WriteReg_ID_EX, WriteReg_MEM_WB;
  wire [5:0] Func;
  wire [9:0] bit_extender_2_out, bit_extender_5_out;
  wire [12:0] CNT_num;
  wire [15:0] Imm16, \LoadUse次数 , \总周期数 , \插入气泡数 , \无条件分支数 , \条件分支成功数 ;
  wire [25:16] Imm26;
  wire [31:0] AluResult, AluResult_EX_MEM, AluResult_MEM_WB, bit_extender_1_out, bit_extender_3_out,
       bit_extender_4_out, BranchValue, EX_IR, ID_IR, IF_IR, Imm16Extend32, Imm16Extend32Shift2, IR,
       IR_EX_MEM, MEM_IR, MemoryOut, MemoryOut_MEM_WB, multiplexer_1_out, multiplexer_2_out,
       multiplexer_8_out, multiplexer_10_out, PCin, PCout, PCoutRaw, PCoutRaw_4, PCoutRaw_4_ID_EX,
       PCoutRaw_4_MEM_WB, PCoutRaw_EX_MEM, PCoutRaw_ID_EX, PCoutRaw_IF_ID, PCoutRaw_MEM_WB, R1, R1_ID_EX, R2,
       R2_ID_EX, shifter_2_out, shifter_3_out, WB_IR;
  wire [31:6] IR_IF_ID;
  wire [31:26] IR_ID_EX;

  Button \u_总复位  (.out(RST));
  Button _1 (.out(IR1));
  Button _2 (.out(IR2));
  Button _3 (.out(IR3));
  // Probe on \总周期数 
  // Probe on \总周期数 
  Button \u_继续运行  (.out(Go));
  LED led_1 (.in(W1));
  LED led_2 (.in(W2));
  LED led_3 (.in(W3));
  Shifter #(.width(32), .shift("lr")) shifter_1 (.in(PCoutRaw), .\dist (5'b00010), .out(PCout));
  Hex_Digit_Display hex_digit_display_1 (.value(LedData[31:28]));  // open: dp
  // Probe on IF_PC[19:0]
  // Mips_Probe mips_probe_1: pin names not known; wires that end beside it: IF_IR
  // Probe on PCoutRaw
  Register #(.width(32)) PC (.D(PCin), .en(1'b1), .Q(PCoutRaw), .clk(CLK), .clr(RST));
  Adder #(.width(32)) adder_1 (.a(PCoutRaw), .b(32'h4), .out(PCoutRaw_4));  // open: cin, cout
  assign bit_extender_1_out = {{6{1'b0}}, {Imm26, Imm16}};  // Bit_Extender bit_extender_1
  Hex_Digit_Display hex_digit_display_2 (.value(LedData[27:24]));  // open: dp
  Hex_Digit_Display hex_digit_display_3 (.value(LedData[23:20]));  // open: dp
  // Probe on ID_PC[19:0]
  // Mips_Probe mips_probe_2: pin names not known; wires that end beside it: ID_IR
  Multiplexer #(.width(32), .enable("false")) multiplexer_1 (
    .in0(PCoutRaw_4), .in1(BranchValue), .out(multiplexer_1_out), .sel(Branch));
  Shifter #(.width(32)) shifter_2 (.in(bit_extender_1_out), .\dist (5'b00010), .out(shifter_2_out));
  // Probe on shifter_2_out
  Hex_Digit_Display hex_digit_display_4 (.value(LedData[15:12]));  // open: dp
  Hex_Digit_Display hex_digit_display_5 (.value(LedData[19:16]));  // open: dp
  // Probe on bit_extender_2_out
  Bit_Extender #(.in_width(32), .out_width(10)) bit_extender_2 (.in(PCout), .out(bit_extender_2_out));
  Multiplexer #(.width(32), .enable("false")) multiplexer_2 (
    .in0(multiplexer_1_out), .in1(shifter_2_out), .out(multiplexer_2_out), .sel(Jmp));
  Shifter #(.width(32)) shifter_3 (.in(R1_ID_EX), .\dist (5'b00010), .out(shifter_3_out));
  Hex_Digit_Display hex_digit_display_6 (.value(LedData[11:8]));  // open: dp
  Hex_Digit_Display hex_digit_display_7 (.value(LedData[7:4]));  // open: dp
  Clock clock_1 (.out(clock_1_out));
  // Probe on EX_PC[19:0]
  // Mips_Probe mips_probe_3: pin names not known; wires that end beside it: clock_1_out, EX_IR, CLK
  Multiplexer #(.width(32), .enable("false")) multiplexer_3 (
    .in0(multiplexer_2_out), .in1(shifter_3_out), .out(PCin), .sel(Jr));
  Hex_Digit_Display hex_digit_display_8 (.value(LedData[3:0]));  // open: dp
  ROM #(.addrWidth(10), .dataWidth(32)) rom_1 (.addr(bit_extender_2_out), .data(IR));  // open: sel
  // Probe on PCin
  // Probe on \总周期数 
  // Probe on M_PC[19:0]
  // Mips_Probe mips_probe_4: pin names not known; wires that end beside it: MEM_IR
  // Mips_Probe mips_probe_5: pin names not known; wires that end beside it: IR, PCoutRaw
  // Probe on \总周期数 
  // Probe on \无条件分支数 
  // Probe on \条件分支成功数 
  // Probe on \插入气泡数 
  // Probe on \LoadUse次数 
  IF_ID if_id_1 (
    .in_1(CLK), .in_2(RST), .in_3(1'b1), .in_5(IR), .out_7({IR_IF_ID, Func}), .out_6(PCoutRaw_IF_ID));  // open: in_4
  // Probe on IF_PC[11:0]
  // Probe on WB_PC[19:0]
  // Mips_Probe mips_probe_6: pin names not known; wires that end beside it: WB_IR
  // Probe on PCoutRaw_IF_ID
  // Probe on {IR_IF_ID, Func}
  // Probe on ID_PC[11:0]
  // Probe on EX_PC[11:0]
  // Probe on M_PC[11:0]
  D_Flip_Flop #(.trigger("high")) d_ff_1 (.Q(d_ff_1_q));  // open: clk, D, Qn, preset, en, reset
  // Probe on 13'hc
  // Probe on WB_PC[11:0]
  Comparator #(.width(13)) comparator_1 (
    .a(CNT_num), .b(13'hc), .eq(comparator_1_eq), .lt(comparator_1_lt));  // open: gt
  Clock clock_2 (.out(clock_2_out));
  // Probe on IR_IF_ID[25:21]
  nand nand_1 (nand_1_out, d_ff_1_q, comparator_1_eq);
  Counter #(.width(13), .max('h1fff), .ongoal("stay")) counter_1 (
    .count(comparator_1_lt), .Q(CNT_num), .clk(clock_2_out));  // open: load, D, carry, clr
  assign CLK = nand_1_out ? clock_2_out : 1'bz;  // Controlled_Buffer controlled_buffer_1
  \单周期硬布线控制器  \u_单周期硬布线控制器_1  (
    .Func(Func), .OP(IR_IF_ID[31:26]), .ALU_OP(AluOp), .MemToReg(MemToReg), .MemWrite(MemWrite),
    .ALU_SRC(AluSrcB), .RegWrite(RegWrite), .SysCALL(Syscall), .SignedExt(SignedExt), .RegDst(RegDst),
    .JR(Jr), .JMP(Jmp), .Beq(Beq), .JAL(Jal), .Bne(Bne));
  Pull_Resistor #(.pull(1)) pull_resistor_1 (.node(CLK));
  // RegisterFile registerfile_1: pin names not known; wires that end beside it: RDin, CLK, RegWrite, WriteReg_MEM_WB, registerfile_1_p5, registerfile_1_p6, R1, R2
  Multiplexer #(.width(5), .enable("false")) multiplexer_4 (
    .in0(IR_IF_ID[25:21]), .in1(5'b00010), .out(registerfile_1_p5), .sel(Syscall));
  Multiplexer #(.width(5), .enable("false")) multiplexer_5 (
    .in0(IR_IF_ID[20:16]), .in1(5'b00100), .out(registerfile_1_p6), .sel(Syscall));
  Multiplexer #(.width(5), .enable("false")) multiplexer_6 (
    .in0(IR_IF_ID[20:16]), .in1(IR_IF_ID[15:11]), .out(multiplexer_6_out), .sel(RegDst));
  Multiplexer #(.width(5), .enable("false")) multiplexer_7 (
    .in0(multiplexer_6_out), .in1({5{1'b1}}), .out(WriteReg), .sel(Jal));
  ID_EX id_ex_1 (
    .in_1(CLK), .in_2(RST), .in_3(1'b1), .in_4(Jmp), .in_5(Jr), .in_6(SignedExt), .in_7(Beq), .in_8(Bne),
    .in_9(MemToReg), .in_10(MemWrite), .in_11(AluOp), .in_12(AluSrcB), .in_13(RegWrite), .in_14(Jal),
    .in_15(RegDst), .in_20(PCoutRaw_IF_ID), .in_21({IR_IF_ID, Func}), .in_22(R1), .in_23(R2),
    .in_25(WriteReg), .out_26(Jmp_ID_EX), .out_27(Jr_ID_EX), .out_28(SignedExt_ID_EX), .out_29(Beq_ID_EX),
    .out_30(Bne_ID_EX), .out_31(MemToReg_ID_EX), .out_32(MemWrite_ID_EX), .out_33(AluOp_ID_EX),
    .out_34(AluSrcB_ID_EX), .out_35(RegWrite_ID_EX), .out_36(Jal_ID_EX), .out_37(RegDst_ID_EX),
    .out_42(PCoutRaw_ID_EX), .out_43({IR_ID_EX, Imm26, Imm16}), .out_44(R1_ID_EX), .out_45(R2_ID_EX),
    .out_47(WriteReg_ID_EX));  // open: in_16, in_17, in_18, in_19, in_24, out_38, out_39, out_40, out_41, out_46
  Multiplexer #(.width(32), .enable("false")) multiplexer_8 (
    .in0(R2_ID_EX), .in1(Imm16Extend32), .out(multiplexer_8_out), .sel(AluSrcB_ID_EX));
  assign bit_extender_3_out = {{16{1'b0}}, Imm16};  // Bit_Extender bit_extender_3
  assign bit_extender_4_out = {{16{Imm16[15]}}, Imm16};  // Bit_Extender bit_extender_4
  Multiplexer #(.width(32), .enable("false")) multiplexer_9 (
    .in0(bit_extender_3_out), .in1(bit_extender_4_out), .out(Imm16Extend32), .sel(SignedExt_ID_EX));
  Shifter #(.width(32)) shifter_4 (.in(bit_extender_4_out), .\dist (5'b00010), .out(Imm16Extend32Shift2));
  Adder #(.width(32)) adder_2 (.a(PCoutRaw_ID_EX), .b(32'h4), .out(PCoutRaw_4_ID_EX));  // open: cin, cout
  Adder #(.width(32)) adder_3 (.a(PCoutRaw_4_ID_EX), .b(Imm16Extend32Shift2), .out(BranchValue));  // open: cin, cout
  and and_1 (and_1_out, Equal, Beq);
  and and_2 (and_2_out, Bne, ~Equal);  // AND_Gate
  MIPS_ALU mips_alu_1 (
    .X(R1_ID_EX), .Y(multiplexer_8_out), .AluOP(AluOp_ID_EX), .Equal(Equal), .Result(AluResult),
    .shamt(Imm16[10:6]));  // open: Result_2
  // Probe on Imm16Extend32Shift2
  or or_1 (Branch, and_1_out, and_2_out);
  // Probe on AluOp_ID_EX
  // Probe on AluResult
  EX_MEM ex_mem_1 (
    .in_1(CLK), .in_2(RST), .in_3(1'b1), .in_4(MemToReg_ID_EX), .in_5(MemWrite_ID_EX), .in_6(RegWrite_ID_EX),
    .in_7(Jal_ID_EX), .in_8(RegDst_ID_EX), .in_11(PCoutRaw_ID_EX), .in_12({IR_ID_EX, Imm26, Imm16}),
    .in_14(R2_ID_EX), .out_17(MemToReg_EX_MEM), .out_18(MemWrite_EX_MEM), .out_19(RegWrite_EX_MEM),
    .out_20(Jal_EX_MEM), .out_21(RegDst_EX_MEM), .out_24(PCoutRaw_EX_MEM), .out_25(IR_EX_MEM), .out_27(MDin),
    .in_15(AluResult), .out_28(AluResult_EX_MEM), .in_16(WriteReg_ID_EX), .out_29(WriteReg_EX_MEM));  // open: in_9, in_10, in_13, out_22, out_23, out_26
  Bit_Extender #(.in_width(32), .out_width(10)) bit_extender_5 (.in(AluResult_EX_MEM), .out(bit_extender_5_out));
  RAM #(.addrWidth(10), .dataWidth(32), .bus("separate")) ram_1 (
    .addr(bit_extender_5_out), .din(MDin), .data(MemoryOut), .str(MemWrite_EX_MEM), .clk(CLK), .clr(RST));  // open: sel, ld
  MEM_WB mem_wb_1 (
    .in_1(CLK), .in_2(RST), .in_3(1'b1), .in_4(MemToReg_EX_MEM), .in_5(RegWrite_EX_MEM), .in_6(Jal_EX_MEM),
    .in_7(RegDst_EX_MEM), .in_8(AluResult_EX_MEM), .in_9(MemoryOut), .out_12(MemToReg_MEM_WB),
    .out_13(RegWrite_MEM_WB), .out_14(Jal_MEM_WB), .out_15(RegDst_MEM_WB), .out_16(AluResult_MEM_WB),
    .out_17(MemoryOut_MEM_WB), .in_11(WriteReg_EX_MEM), .out_19(WriteReg_MEM_WB), .in_10(PCoutRaw_EX_MEM),
    .out_18(PCoutRaw_MEM_WB));
  Adder #(.width(32)) adder_4 (.a(PCoutRaw_MEM_WB), .b(32'h4), .out(PCoutRaw_4_MEM_WB));  // open: cin, cout
  Multiplexer #(.width(32), .enable("false")) multiplexer_10 (
    .in0(AluResult_MEM_WB), .in1(MemoryOut_MEM_WB), .out(multiplexer_10_out), .sel(MemToReg_MEM_WB));
  Multiplexer #(.width(32), .enable("false")) multiplexer_11 (
    .in0(multiplexer_10_out), .in1(PCoutRaw_MEM_WB), .out(RDin), .sel(Jal_MEM_WB));

  // Other names for the same wires on the sheet: Imm26[15:0] = Imm16; IR_ID_EX[25:0] = {Imm26, Imm16};
  //   shamt[4:0] = Imm16[10:6]; IR_IF_ID[5:0] = Func; rd[4:0] = IR_IF_ID[15:11]; rt[4:0] = IR_IF_ID[20:16];
  //   rs[4:0] = IR_IF_ID[25:21]; OP[5:0] = IR_IF_ID[31:26]; MEM_PC[31:0] = M_PC; R2_EX_MEM[31:0] = MDin;
  //   WriteBackData[31:0] = RDin

  // Notes on the sheet:
  //   中断源
  //   时空图监测，可删除
  //   中断等待指示
  //   数码管输出
  //   指令存储器
  //   contents of rom_1 (hex, n*v repeats v):
  //   2010ffff 20110000 ae300200 22100001 22310004 ae300200 22100001 22310004 ae300200 22100001 22310004
  //   ae300200 22100001 22310004 ae300200 22100001 22310004 ae300200 22100001 22310004 ae300200 22100001
  //   22310004 ae300200 8020 2011001c 8e130200 8e340200 274402a 11000002 ae330200 ae140200 2231fffc
  //   1611fff8 22100004 2011001c 1611fff5 2002000a c
  //   OP
  //   指令字
  //   控制位
  //   流水调试日志用
  //   暂停节拍，不能为0
  //   Func
  //   rs
  //   rt
  //   rd
  //   戳工具置1进入计数暂停模式，ctrl+k时钟自动运行到对应节拍暂停
  //   ctrl+k关闭时钟连续运行，将控制位置零，进入单步调试模式调试
  //   用这个时钟源需要去掉电路中的其他时钟源
  //   可计数暂停的时钟源
  //   Beq
  //   JMP
  //   JR
  //   Bne
  //   OP
  //   JAL
  //   Func
  //   Syscall
  //   MemToReg
  //   MemWrite
  //   AluOP
  //   AluSrcB
  //   RegWrite
  //   RegDst
  //   为方便自动评测，需要输出流水线各段保存的PC值，注意是PC不是PC+4，另外ID段寄存器写入信息，Mem段内存写入信息也要输出
endmodule

module \气泡流水线  (
  output RegWrite,
  output MemWrite,
  output [31:0] IF_PC,
  output [31:0] ID_PC,
  output [31:0] EX_PC,
  output [31:0] M_PC,
  output [31:0] WB_PC,
  output [31:0] RDin,
  output [31:0] MDin,
  output [31:0] LedData
);

  wire CLK, clock_2_out, comparator_1_eq, comparator_1_lt, d_ff_1_q, Go, IR1, IR2, IR3, nand_1_out, RST, W1,
       W2, W3;
  wire [12:0] CNT_num;
  wire [15:0] \LoadUse次数 , \总周期数 , \插入气泡数 , \无条件分支数 , \条件分支成功数 ;
  wire [31:0] EX_IR, ID_IR, IF_IR, MEM_IR, WB_IR;

  Button \u_总复位  (.out(RST));
  Button _1 (.out(IR1));
  Button _2 (.out(IR2));
  Button _3 (.out(IR3));
  // Probe on \总周期数 
  // Probe on \总周期数 
  Button \u_继续运行  (.out(Go));
  LED led_1 (.in(W1));
  LED led_2 (.in(W2));
  LED led_3 (.in(W3));
  Hex_Digit_Display hex_digit_display_1 (.value(LedData[31:28]));  // open: dp
  // Probe on IF_PC[19:0]
  // Mips_Probe mips_probe_1: pin names not known; wires that end beside it: IF_IR
  Hex_Digit_Display hex_digit_display_2 (.value(LedData[27:24]));  // open: dp
  Hex_Digit_Display hex_digit_display_3 (.value(LedData[23:20]));  // open: dp
  // Probe on ID_PC[19:0]
  // Mips_Probe mips_probe_2: pin names not known; wires that end beside it: ID_IR
  Hex_Digit_Display hex_digit_display_4 (.value(LedData[19:16]));  // open: dp
  Hex_Digit_Display hex_digit_display_5 (.value(LedData[15:12]));  // open: dp
  Hex_Digit_Display hex_digit_display_6 (.value(LedData[11:8]));  // open: dp
  Hex_Digit_Display hex_digit_display_7 (.value(LedData[7:4]));  // open: dp
  Clock clock_1 (.out(CLK));
  // Probe on EX_PC[19:0]
  // Mips_Probe mips_probe_3: pin names not known; wires that end beside it: EX_IR
  Hex_Digit_Display hex_digit_display_8 (.value(LedData[3:0]));  // open: dp
  // Probe on \总周期数 
  // Probe on M_PC[19:0]
  // Mips_Probe mips_probe_4: pin names not known; wires that end beside it: MEM_IR
  // Probe on \总周期数 
  // Probe on \无条件分支数 
  // Probe on \条件分支成功数 
  // Probe on \插入气泡数 
  // Probe on \LoadUse次数 
  // Probe on IF_PC[11:0]
  // Probe on WB_PC[19:0]
  // Mips_Probe mips_probe_5: pin names not known; wires that end beside it: WB_IR
  // Probe on ID_PC[11:0]
  // Probe on EX_PC[11:0]
  // Probe on M_PC[11:0]
  D_Flip_Flop #(.trigger("high")) d_ff_1 (.Q(d_ff_1_q));  // open: clk, D, Qn, preset, en, reset
  // Probe on 13'hc
  // Probe on WB_PC[11:0]
  Comparator #(.width(13)) comparator_1 (
    .a(CNT_num), .b(13'hc), .eq(comparator_1_eq), .lt(comparator_1_lt));  // open: gt
  Clock clock_2 (.out(clock_2_out));
  nand nand_1 (nand_1_out, d_ff_1_q, comparator_1_eq);
  Counter #(.width(13), .max('h1fff), .ongoal("stay")) counter_1 (
    .count(comparator_1_lt), .Q(CNT_num), .clk(clock_2_out));  // open: load, D, carry, clr
  assign CLK = nand_1_out ? clock_2_out : 1'bz;  // Controlled_Buffer controlled_buffer_1
  Pull_Resistor #(.pull(1)) pull_resistor_1 (.node(CLK));

  // Other names for the same wires on the sheet: MEM_PC[31:0] = M_PC

  // Notes on the sheet:
  //   中断源
  //   时空图监测，可删除
  //   中断等待指示
  //   数码管输出
  //   控制位
  //   流水调试日志用
  //   暂停节拍，不能为0
  //   戳工具置1进入计数暂停模式，ctrl+k时钟自动运行到对应节拍暂停
  //   ctrl+k关闭时钟连续运行，将控制位置零，进入单步调试模式调试
  //   可计数暂停的时钟源
  //   为方便自动评测，需要输出流水线各段保存的PC值，注意是PC不是PC+4，另外ID段寄存器写入信息，Mem段内存写入信息也要输出
endmodule

module \重定向流水线  (
  output RegWrite,
  output MemWrite,
  output [31:0] IF_PC,
  output [31:0] ID_PC,
  output [31:0] EX_PC,
  output [31:0] M_PC,
  output [31:0] WB_PC,
  output [31:0] RDin,
  output [31:0] MDin,
  output [31:0] LedData
);

  wire CLK, clock_2_out, comparator_1_eq, comparator_1_lt, d_ff_1_q, Go, IR1, IR2, IR3, nand_1_out, RST, W1,
       W2, W3;
  wire [12:0] CNT_num;
  wire [15:0] \LoadUse次数 , \总周期数 , \插入气泡数 , \无条件分支数 , \条件分支成功数 ;
  wire [31:0] EX_IR, ID_IR, IF_IR, MEM_IR, WB_IR;

  Button \u_总复位  (.out(RST));
  Button _1 (.out(IR1));
  Button _2 (.out(IR2));
  Button _3 (.out(IR3));
  // Probe on \总周期数 
  // Probe on \总周期数 
  Button \u_继续运行  (.out(Go));
  LED led_1 (.in(W1));
  LED led_2 (.in(W2));
  LED led_3 (.in(W3));
  Hex_Digit_Display hex_digit_display_1 (.value(LedData[31:28]));  // open: dp
  // Probe on IF_PC[19:0]
  // Mips_Probe mips_probe_1: pin names not known; wires that end beside it: IF_IR
  Hex_Digit_Display hex_digit_display_2 (.value(LedData[27:24]));  // open: dp
  Hex_Digit_Display hex_digit_display_3 (.value(LedData[23:20]));  // open: dp
  // Probe on ID_PC[19:0]
  // Mips_Probe mips_probe_2: pin names not known; wires that end beside it: ID_IR
  Hex_Digit_Display hex_digit_display_4 (.value(LedData[15:12]));  // open: dp
  Hex_Digit_Display hex_digit_display_5 (.value(LedData[19:16]));  // open: dp
  Hex_Digit_Display hex_digit_display_6 (.value(LedData[11:8]));  // open: dp
  Hex_Digit_Display hex_digit_display_7 (.value(LedData[7:4]));  // open: dp
  Clock clock_1 (.out(CLK));
  // Probe on EX_PC[19:0]
  // Mips_Probe mips_probe_3: pin names not known; wires that end beside it: EX_IR
  Hex_Digit_Display hex_digit_display_8 (.value(LedData[3:0]));  // open: dp
  // Probe on \总周期数 
  // Probe on M_PC[19:0]
  // Mips_Probe mips_probe_4: pin names not known; wires that end beside it: MEM_IR
  // Probe on \总周期数 
  // Probe on \无条件分支数 
  // Probe on \条件分支成功数 
  // Probe on \插入气泡数 
  // Probe on \LoadUse次数 
  // Probe on IF_PC[11:0]
  // Probe on WB_PC[19:0]
  // Mips_Probe mips_probe_5: pin names not known; wires that end beside it: WB_IR
  // Probe on EX_PC[11:0]
  // Probe on ID_PC[11:0]
  // Probe on M_PC[11:0]
  D_Flip_Flop #(.trigger("high")) d_ff_1 (.Q(d_ff_1_q));  // open: clk, D, Qn, preset, en, reset
  // Probe on 13'hc
  // Probe on WB_PC[11:0]
  Comparator #(.width(13)) comparator_1 (
    .a(CNT_num), .b(13'hc), .eq(comparator_1_eq), .lt(comparator_1_lt));  // open: gt
  Clock clock_2 (.out(clock_2_out));
  nand nand_1 (nand_1_out, d_ff_1_q, comparator_1_eq);
  Counter #(.width(13), .max('h1fff), .ongoal("stay")) counter_1 (
    .count(comparator_1_lt), .Q(CNT_num), .clk(clock_2_out));  // open: load, D, carry, clr
  assign CLK = nand_1_out ? clock_2_out : 1'bz;  // Controlled_Buffer controlled_buffer_1
  Pull_Resistor #(.pull(1)) pull_resistor_1 (.node(CLK));

  // Other names for the same wires on the sheet: MEM_PC[31:0] = M_PC

  // Notes on the sheet:
  //   中断源
  //   时空图监测，可删除
  //   中断等待指示
  //   数码管输出
  //   控制位
  //   流水调试日志用
  //   暂停节拍，不能为0
  //   戳工具置1进入计数暂停模式，ctrl+k时钟自动运行到对应节拍暂停
  //   ctrl+k关闭时钟连续运行，将控制位置零，进入单步调试模式调试
  //   可计数暂停的时钟源
  //   为方便自动评测，需要输出流水线各段保存的PC值，注意是PC不是PC+4，另外ID段寄存器写入信息，Mem段内存写入信息也要输出
endmodule

module \中断按键参考电路  (
  input  \同步清零信号 ,
  output \与中断屏蔽位与 
);

  wire \_1号中断_out , and_1_out, clock_1_out, d_ff_1_q, or_1_out, or_2_out;

  Clock clock_1 (.out(clock_1_out));
  Button \_1号中断  (.out(\_1号中断_out ));
  or or_1 (or_1_out, \与中断屏蔽位与 , d_ff_1_q);
  LED \_1号中断等待指示灯  (.in(or_1_out));
  D_Flip_Flop d_ff_1 (.clk(\_1号中断_out ), .D(1'b1), .Q(d_ff_1_q), .reset(\与中断屏蔽位与 ));  // open: Qn, preset, en
  or or_2 (or_2_out, d_ff_1_q, \与中断屏蔽位与 );
  and and_1 (and_1_out, or_2_out, ~\同步清零信号 );  // AND_Gate
  D_Flip_Flop IR1 (.clk(clock_1_out), .D(and_1_out), .Q(\与中断屏蔽位与 ));  // open: Qn, preset, en, reset
  \单周期硬布线控制器  \u_单周期硬布线控制器_1  ();  // open: Func, OP, ALU_OP, MemToReg, MemWrite, ALU_SRC, RegWrite, SysCALL, SignedExt, RegDst, JR, JMP, Beq, JAL, Bne

  // Notes on the sheet:
  //   中断信号采样参考电路
  //   Reset 
endmodule

module \单周期MIPS_单级中断  (
  input  IR1,
  input  IR2,
  input  IR3,
  output RegWrite,
  output MemWrite,
  output [31:0] PC,
  output [31:0] IR,
  output [31:0] RDin,
  output [31:0] MDin,
  output [31:0] LedData
);

  wire CLK, comparator_1_eq, comparator_2_eq, comparator_3_eq, comparator_4_eq, Go, IR1_t, IR2_t, IR3_t, IRA,
       IRB, IRC, or_1_out, W1, W2, W3;
  wire [15:0] \总周期数 ;

  Clock clock_1 (.out(CLK));
  Button _1 ();  // open: out
  Button _2 ();  // open: out
  Button _3 ();  // open: out
  Button \u_继续运行  (.out(Go));
  LED led_1 (.in(W1));
  LED led_2 (.in(W2));
  LED led_3 (.in(W3));
  Hex_Digit_Display hex_digit_display_1 (.value(LedData[31:28]));  // open: dp
  Comparator #(.width(16)) comparator_1 (.a(16'h23b), .b(\总周期数 ), .eq(comparator_1_eq));  // open: gt, lt
  Comparator #(.width(16)) comparator_2 (.a(\总周期数 ), .b(16'h1), .eq(comparator_2_eq));  // open: gt, lt
  Comparator #(.width(16)) comparator_3 (.a(\总周期数 ), .b(16'h4), .eq(comparator_3_eq));  // open: gt, lt
  Comparator #(.width(16)) comparator_4 (.a(\总周期数 ), .b(16'h7), .eq(comparator_4_eq));  // open: gt, lt
  Hex_Digit_Display hex_digit_display_2 (.value(LedData[23:20]));  // open: dp
  Hex_Digit_Display hex_digit_display_3 (.value(LedData[27:24]));  // open: dp
  or or_1 (or_1_out, comparator_1_eq, comparator_2_eq);
  assign IRA = or_1_out ? ~CLK : 1'bz;  // Controlled_Inverter controlled_inverter_1
  assign IRB = comparator_3_eq ? ~CLK : 1'bz;  // Controlled_Inverter controlled_inverter_2
  assign IRC = comparator_4_eq ? ~CLK : 1'bz;  // Controlled_Inverter controlled_inverter_3
  Hex_Digit_Display hex_digit_display_4 (.value(LedData[15:12]));  // open: dp
  Hex_Digit_Display hex_digit_display_5 (.value(LedData[19:16]));  // open: dp
  Pull_Resistor pull_resistor_1 (.node(IRA));
  Pull_Resistor pull_resistor_2 (.node(IRB));
  Pull_Resistor pull_resistor_3 (.node(IRC));
  Hex_Digit_Display hex_digit_display_6 (.value(LedData[7:4]));  // open: dp
  Hex_Digit_Display hex_digit_display_7 (.value(LedData[11:8]));  // open: dp
  // Probe on \总周期数 
  Hex_Digit_Display hex_digit_display_8 (.value(LedData[3:0]));  // open: dp
  or or_2 (IR1_t, IR1, IRA);
  or or_3 (IR2_t, IR2, IRB);
  or or_4 (IR3_t, IR3, IRC);

  // Notes on the sheet:
  //   中断源
  //   中断等待指示
  //   总复位信号应将除ROM以外所有存储组件全部清零
  //   单级中断测试信号模拟器
  //   数码管输出
  //   数码管输出应该用寄存器锁存，否则显示数据只能一闪而过
  //   为方便自动评测，需要输出PC，IR，寄存器堆写如数据RDin
  //   RAM写使能MemWrite、RAM写入数据MDin等信号
endmodule

module \单周期MIPS_多级中断  (
  input  IR1,
  input  IR2,
  input  IR3,
  output RegWrite,
  output MemWrite,
  output [31:0] PC,
  output [31:0] IR,
  output [31:0] RDin,
  output [31:0] MDin,
  output [31:0] LedData
);

  wire CLK, comparator_1_eq, comparator_2_eq, comparator_3_eq, comparator_4_eq, comparator_5_eq, Go, IR1_t,
       IR2_t, IR3_t, IRA, IRB, IRC, or_1_out, or_2_out, W1, W2, W3;
  wire [15:0] \总周期数 ;

  Clock clock_1 (.out(CLK));
  Button _1 ();  // open: out
  Button _2 ();  // open: out
  Button _3 ();  // open: out
  Button \u_继续运行  (.out(Go));
  LED led_1 (.in(W1));
  LED led_2 (.in(W2));
  LED led_3 (.in(W3));
  Hex_Digit_Display hex_digit_display_1 (.value(LedData[31:28]));  // open: dp
  Comparator #(.width(16)) comparator_1 (.a(\总周期数 ), .b(16'h7), .eq(comparator_1_eq));  // open: gt, lt
  Comparator #(.width(16)) comparator_2 (.a(\总周期数 ), .b(16'h241), .eq(comparator_2_eq));  // open: gt, lt
  Hex_Digit_Display hex_digit_display_2 (.value(LedData[23:20]));  // open: dp
  Hex_Digit_Display hex_digit_display_3 (.value(LedData[27:24]));  // open: dp
  Comparator #(.width(16)) comparator_3 (.a(16'h258), .b(\总周期数 ), .eq(comparator_3_eq));  // open: gt, lt
  or or_1 (or_1_out, comparator_3_eq, comparator_4_eq);
  Comparator #(.width(16)) comparator_4 (.a(\总周期数 ), .b(16'h1), .eq(comparator_4_eq));  // open: gt, lt
  Comparator #(.width(16)) comparator_5 (.a(\总周期数 ), .b(16'h4), .eq(comparator_5_eq));  // open: gt, lt
  or or_2 (or_2_out, comparator_1_eq, comparator_2_eq);
  Hex_Digit_Display hex_digit_display_4 (.value(LedData[19:16]));  // open: dp
  Hex_Digit_Display hex_digit_display_5 (.value(LedData[15:12]));  // open: dp
  Pull_Resistor pull_resistor_1 (.node(IRA));
  assign IRA = or_1_out ? ~CLK : 1'bz;  // Controlled_Inverter controlled_inverter_1
  Pull_Resistor pull_resistor_2 (.node(IRB));
  assign IRB = comparator_5_eq ? ~CLK : 1'bz;  // Controlled_Inverter controlled_inverter_2
  Pull_Resistor pull_resistor_3 (.node(IRC));
  assign IRC = or_2_out ? ~CLK : 1'bz;  // Controlled_Inverter controlled_inverter_3
  Hex_Digit_Display hex_digit_display_6 (.value(LedData[11:8]));  // open: dp
  Hex_Digit_Display hex_digit_display_7 (.value(LedData[7:4]));  // open: dp
  // Probe on \总周期数 
  Hex_Digit_Display hex_digit_display_8 (.value(LedData[3:0]));  // open: dp
  or or_3 (IR1_t, IR1, IRA);
  or or_4 (IR2_t, IR2, IRB);
  or or_5 (IR3_t, IR3, IRC);

  // Notes on the sheet:
  //   中断源
  //   中断等待指示
  //   总复位信号应将除ROM以外所有存储组件全部清零
  //   多级中断测试信号模拟器
  //   数码管输出
  //   数码管输出应该用寄存器锁存，否则显示数据只能一闪而过
  //   为方便自动评测，需要输出PC，IR，寄存器堆写如数据RDin
  //   RAM写使能MemWrite、RAM写入数据MDin等信号
endmodule

module \封装正确性测试  (
);

  wire IR1, IR2, IR3, MemW, RegW;
  wire [31:0] EX_PC, ID_PC, IF_PC, IR, LED, MDin, MDinr, MEM_PC, PC, RDin, RDinr, WB_PC;

  \单周期MIPS  \u_单周期mips_1  (
    .RegWrite(RegW), .MemWrite(MemW), .PC(PC), .IR(IR), .RDin(RDin), .MDin(MDin), .LedData(LED));  // open: IR1, IR2, IR3
  \气泡流水线  \u_气泡流水线_1  (
    .RegWrite(RegW), .MemWrite(MemW), .IF_PC(IF_PC), .ID_PC(ID_PC), .EX_PC(EX_PC), .M_PC(MEM_PC),
    .WB_PC(WB_PC), .RDin(RDinr), .MDin(MDinr), .LedData(LED));
  \单周期MIPS_单级中断  \u_单周期mips_单级中断_1  (
    .IR1(IR1), .IR2(IR2), .IR3(IR3), .RegWrite(RegW), .MemWrite(MemW), .PC(PC), .IR(IR), .RDin(RDin),
    .MDin(MDin), .LedData(LED));
  \理想流水线  \u_理想流水线_1  (
    .RegWrite(RegW), .MemWrite(MemW), .IF_PC(IF_PC), .ID_PC(ID_PC), .EX_PC(EX_PC), .M_PC(MEM_PC),
    .WB_PC(WB_PC), .RDin(RDinr), .MDin(MDinr), .LedData(LED));
  \重定向流水线  \u_重定向流水线_1  (
    .RegWrite(RegW), .MemWrite(MemW), .IF_PC(IF_PC), .ID_PC(ID_PC), .EX_PC(EX_PC), .M_PC(MEM_PC),
    .WB_PC(WB_PC), .RDin(RDinr), .MDin(MDinr), .LedData(LED));
  \单周期MIPS_多级中断  \u_单周期mips_多级中断_1  (
    .IR1(IR1), .IR2(IR2), .IR3(IR3), .RegWrite(RegW), .MemWrite(MemW), .PC(PC), .IR(IR), .RDin(RDin),
    .MDin(MDin), .LedData(LED));

  // Notes on the sheet:
  //   单周期封装测试
  //   气泡流水封装测试
  //   单周期+单级中断封装测试
  //   请检查上面封装有无位宽不匹配，引脚标签是否和连接的标签相对应，否则无法在educoder平台上正确测试
  //   理想流水封装测试
  //   重定向流水封装测试
  //   单周期+多级中断封装测试
endmodule

module IF_ID (
  input  in_1,
  input  in_2,
  input  in_3,
  input  [31:0] in_4,
  input  [31:0] in_5,
  output [31:0] out_6,
  output [31:0] out_7
);

  wire [31:0] multiplexer_1_out, multiplexer_2_out;

  Multiplexer #(.width(32), .enable("false")) multiplexer_1 (
    .in0(in_4), .in1({32{1'b0}}), .out(multiplexer_1_out), .sel(in_2));
  Multiplexer #(.width(32), .enable("false")) multiplexer_2 (
    .in0(in_5), .in1({32{1'b0}}), .out(multiplexer_2_out), .sel(in_2));
  Register #(.width(32)) register_1 (.D(multiplexer_1_out), .en(in_3), .Q(out_6), .clk(in_1), .clr(in_2));
  Register #(.width(32)) register_2 (.D(multiplexer_2_out), .en(in_3), .Q(out_7), .clk(in_1), .clr(in_2));

  // Other names for the same wires on the sheet: CLK = in_1; EN = in_3; RST = in_2
endmodule

module ID_EX (
  input  in_1,
  input  in_2,
  input  in_3,
  input  in_4,
  input  in_5,
  input  in_6,
  input  in_7,
  input  in_8,
  input  in_9,
  input  in_10,
  input  [3:0] in_11,
  input  in_12,
  input  in_13,
  input  in_14,
  input  in_15,
  input  in_16,
  input  in_17,
  input  in_18,
  input  [4:0] in_19,
  input  [31:0] in_20,
  input  [31:0] in_21,
  input  [31:0] in_22,
  input  [31:0] in_23,
  input  [25:0] in_24,
  input  [4:0] in_25,
  output out_26,
  output out_27,
  output out_28,
  output out_29,
  output out_30,
  output out_31,
  output out_32,
  output [3:0] out_33,
  output out_34,
  output out_35,
  output out_36,
  output out_37,
  output out_38,
  output out_39,
  output out_40,
  output [4:0] out_41,
  output [31:0] out_42,
  output [31:0] out_43,
  output [31:0] out_44,
  output [31:0] out_45,
  output [25:0] out_46,
  output [4:0] out_47
);

  wire multiplexer_1_out, multiplexer_2_out, multiplexer_3_out, multiplexer_4_out, multiplexer_8_out,
       multiplexer_9_out, multiplexer_10_out, multiplexer_11_out, multiplexer_12_out, multiplexer_13_out,
       multiplexer_14_out, multiplexer_15_out, multiplexer_19_out, multiplexer_21_out;
  wire [3:0] multiplexer_20_out;
  wire [4:0] multiplexer_18_out, multiplexer_22_out;
  wire [25:0] multiplexer_7_out;
  wire [31:0] multiplexer_5_out, multiplexer_6_out, multiplexer_16_out, multiplexer_17_out;

  Multiplexer #(.enable("false")) multiplexer_1 (.in0(in_4), .in1(1'b0), .out(multiplexer_1_out), .sel(in_2));
  Multiplexer #(.enable("false")) multiplexer_2 (.in0(in_8), .in1(1'b0), .out(multiplexer_2_out), .sel(in_2));
  Multiplexer #(.enable("false")) multiplexer_3 (.in0(in_12), .in1(1'b0), .out(multiplexer_3_out), .sel(in_2));
  Multiplexer #(.enable("false")) multiplexer_4 (.in0(in_16), .in1(1'b0), .out(multiplexer_4_out), .sel(in_2));
  Register #(.width(1)) register_1 (.D(multiplexer_1_out), .en(in_3), .Q(out_26), .clk(in_1), .clr(in_2));
  Register #(.width(1)) register_2 (.D(multiplexer_2_out), .en(in_3), .Q(out_30), .clk(in_1), .clr(in_2));
  Register #(.width(1)) register_3 (.D(multiplexer_3_out), .en(in_3), .Q(out_34), .clk(in_1), .clr(in_2));
  Register #(.width(1)) register_4 (.D(multiplexer_4_out), .en(in_3), .Q(out_38), .clk(in_1), .clr(in_2));
  Multiplexer #(.width(32), .enable("false")) multiplexer_5 (
    .in0(in_20), .in1({32{1'b0}}), .out(multiplexer_5_out), .sel(in_2));
  Register #(.width(32)) register_5 (.D(multiplexer_5_out), .en(in_3), .Q(out_42), .clk(in_1), .clr(in_2));
  Multiplexer #(.width(32), .enable("false")) multiplexer_6 (
    .in0(in_22), .in1({32{1'b0}}), .out(multiplexer_6_out), .sel(in_2));
  Register #(.width(32)) register_6 (.D(multiplexer_6_out), .en(in_3), .Q(out_44), .clk(in_1), .clr(in_2));
  Register #(.width(26)) register_7 (.D(multiplexer_7_out), .en(in_3), .Q(out_46), .clk(in_1), .clr(in_2));
  Multiplexer #(.width(26), .enable("false")) multiplexer_7 (
    .in0(in_24), .in1({26{1'b0}}), .out(multiplexer_7_out), .sel(in_2));
  Multiplexer #(.enable("false")) multiplexer_8 (.in0(in_5), .in1(1'b0), .out(multiplexer_8_out), .sel(in_2));
  Multiplexer #(.enable("false")) multiplexer_9 (.in0(in_9), .in1(1'b0), .out(multiplexer_9_out), .sel(in_2));
  Multiplexer #(.enable("false")) multiplexer_10 (.in0(in_13), .in1(1'b0), .out(multiplexer_10_out), .sel(in_2));
  Multiplexer #(.enable("false")) multiplexer_11 (.in0(in_17), .in1(1'b0), .out(multiplexer_11_out), .sel(in_2));
  Register #(.width(1)) register_8 (.D(multiplexer_8_out), .en(in_3), .Q(out_27), .clk(in_1), .clr(in_2));
  Register #(.width(1)) register_9 (.D(multiplexer_9_out), .en(in_3), .Q(out_31), .clk(in_1), .clr(in_2));
  Register #(.width(1)) register_10 (.D(multiplexer_10_out), .en(in_3), .Q(out_35), .clk(in_1), .clr(in_2));
  Register #(.width(1)) register_11 (.D(multiplexer_11_out), .en(in_3), .Q(out_39), .clk(in_1), .clr(in_2));
  Register #(.width(1)) register_12 (.D(multiplexer_12_out), .en(in_3), .Q(out_28), .clk(in_1), .clr(in_2));
  Multiplexer #(.enable("false")) multiplexer_12 (.in0(in_6), .in1(1'b0), .out(multiplexer_12_out), .sel(in_2));
  Register #(.width(1)) register_13 (.D(multiplexer_13_out), .en(in_3), .Q(out_32), .clk(in_1), .clr(in_2));
  Multiplexer #(.enable("false")) multiplexer_13 (.in0(in_10), .in1(1'b0), .out(multiplexer_13_out), .sel(in_2));
  Register #(.width(1)) register_14 (.D(multiplexer_14_out), .en(in_3), .Q(out_36), .clk(in_1), .clr(in_2));
  Multiplexer #(.enable("false")) multiplexer_14 (.in0(in_14), .in1(1'b0), .out(multiplexer_14_out), .sel(in_2));
  Multiplexer #(.enable("false")) multiplexer_15 (.in0(in_18), .in1(1'b0), .out(multiplexer_15_out), .sel(in_2));
  Register #(.width(1)) register_15 (.D(multiplexer_15_out), .en(in_3), .Q(out_40), .clk(in_1), .clr(in_2));
  Multiplexer #(.width(32), .enable("false")) multiplexer_16 (
    .in0(in_21), .in1({32{1'b0}}), .out(multiplexer_16_out), .sel(in_2));
  Multiplexer #(.width(32), .enable("false")) multiplexer_17 (
    .in0(in_23), .in1({32{1'b0}}), .out(multiplexer_17_out), .sel(in_2));
  Multiplexer #(.width(5), .enable("false")) multiplexer_18 (
    .in0(in_25), .in1({5{1'b0}}), .out(multiplexer_18_out), .sel(in_2));
  Multiplexer #(.enable("false")) multiplexer_19 (.in0(in_7), .in1(1'b0), .out(multiplexer_19_out), .sel(in_2));
  Multiplexer #(.width(4), .enable("false")) multiplexer_20 (
    .in0(in_11), .in1(4'b0000), .out(multiplexer_20_out), .sel(in_2));
  Multiplexer #(.enable("false")) multiplexer_21 (.in0(in_15), .in1(1'b0), .out(multiplexer_21_out), .sel(in_2));
  Multiplexer #(.width(5), .enable("false")) multiplexer_22 (
    .in0(in_19), .in1({5{1'b0}}), .out(multiplexer_22_out), .sel(in_2));
  Register #(.width(32)) register_16 (.D(multiplexer_16_out), .en(in_3), .Q(out_43), .clk(in_1), .clr(in_2));
  Register #(.width(32)) register_17 (.D(multiplexer_17_out), .en(in_3), .Q(out_45), .clk(in_1), .clr(in_2));
  Register #(.width(5)) register_18 (.D(multiplexer_18_out), .en(in_3), .Q(out_47), .clk(in_1), .clr(in_2));
  Register #(.width(1)) register_19 (.D(multiplexer_19_out), .en(in_3), .Q(out_29), .clk(in_1), .clr(in_2));
  Register #(.width(4)) register_20 (.D(multiplexer_20_out), .en(in_3), .Q(out_33), .clk(in_1), .clr(in_2));
  Register #(.width(1)) register_21 (.D(multiplexer_21_out), .en(in_3), .Q(out_37), .clk(in_1), .clr(in_2));
  Register #(.width(5)) register_22 (.D(multiplexer_22_out), .en(in_3), .Q(out_41), .clk(in_1), .clr(in_2));

  // Other names for the same wires on the sheet: CLK = in_1; EN = in_3; RST = in_2
endmodule

module EX_MEM (
  input  in_1,
  input  in_2,
  input  in_3,
  input  in_4,
  input  in_5,
  input  in_6,
  input  in_7,
  input  in_8,
  input  in_9,
  input  in_10,
  input  [31:0] in_11,
  input  [31:0] in_12,
  input  [31:0] in_13,
  input  [31:0] in_14,
  input  [31:0] in_15,
  input  [4:0] in_16,
  output out_17,
  output out_18,
  output out_19,
  output out_20,
  output out_21,
  output out_22,
  output out_23,
  output [31:0] out_24,
  output [31:0] out_25,
  output [31:0] out_26,
  output [31:0] out_27,
  output [31:0] out_28,
  output [4:0] out_29
);

  wire multiplexer_1_out, multiplexer_2_out, multiplexer_6_out, multiplexer_7_out, multiplexer_8_out,
       multiplexer_9_out, multiplexer_13_out;
  wire [4:0] multiplexer_12_out;
  wire [31:0] multiplexer_3_out, multiplexer_4_out, multiplexer_5_out, multiplexer_10_out, multiplexer_11_out;

  Multiplexer #(.enable("false")) multiplexer_1 (.in0(in_4), .in1(1'b0), .out(multiplexer_1_out), .sel(in_2));
  Multiplexer #(.enable("false")) multiplexer_2 (.in0(in_8), .in1(1'b0), .out(multiplexer_2_out), .sel(in_2));
  Register #(.width(1)) register_1 (.D(multiplexer_1_out), .en(in_3), .Q(out_17), .clk(in_1), .clr(in_2));
  Register #(.width(1)) register_2 (.D(multiplexer_2_out), .en(in_3), .Q(out_21), .clk(in_1), .clr(in_2));
  Multiplexer #(.width(32), .enable("false")) multiplexer_3 (
    .in0(in_11), .in1({32{1'b0}}), .out(multiplexer_3_out), .sel(in_2));
  Register #(.width(32)) register_3 (.D(multiplexer_3_out), .en(in_3), .Q(out_24), .clk(in_1), .clr(in_2));
  Register #(.width(32)) register_4 (.D(multiplexer_4_out), .en(in_3), .Q(out_26), .clk(in_1), .clr(in_2));
  Multiplexer #(.width(32), .enable("false")) multiplexer_4 (
    .in0(in_13), .in1({32{1'b0}}), .out(multiplexer_4_out), .sel(in_2));
  Register #(.width(32)) register_5 (.D(multiplexer_5_out), .en(in_3), .Q(out_28), .clk(in_1), .clr(in_2));
  Multiplexer #(.width(32), .enable("false")) multiplexer_5 (
    .in0(in_15), .in1({32{1'b0}}), .out(multiplexer_5_out), .sel(in_2));
  Multiplexer #(.enable("false")) multiplexer_6 (.in0(in_5), .in1(1'b0), .out(multiplexer_6_out), .sel(in_2));
  Multiplexer #(.enable("false")) multiplexer_7 (.in0(in_9), .in1(1'b0), .out(multiplexer_7_out), .sel(in_2));
  Register #(.width(1)) register_6 (.D(multiplexer_6_out), .en(in_3), .Q(out_18), .clk(in_1), .clr(in_2));
  Register #(.width(1)) register_7 (.D(multiplexer_7_out), .en(in_3), .Q(out_22), .clk(in_1), .clr(in_2));
  Multiplexer #(.enable("false")) multiplexer_8 (.in0(in_6), .in1(1'b0), .out(multiplexer_8_out), .sel(in_2));
  Register #(.width(1)) register_8 (.D(multiplexer_8_out), .en(in_3), .Q(out_19), .clk(in_1), .clr(in_2));
  Register #(.width(1)) register_9 (.D(multiplexer_9_out), .en(in_3), .Q(out_23), .clk(in_1), .clr(in_2));
  Multiplexer #(.enable("false")) multiplexer_9 (.in0(in_10), .in1(1'b0), .out(multiplexer_9_out), .sel(in_2));
  Multiplexer #(.width(32), .enable("false")) multiplexer_10 (
    .in0(in_12), .in1({32{1'b0}}), .out(multiplexer_10_out), .sel(in_2));
  Multiplexer #(.width(32), .enable("false")) multiplexer_11 (
    .in0(in_14), .in1({32{1'b0}}), .out(multiplexer_11_out), .sel(in_2));
  Multiplexer #(.width(5), .enable("false")) multiplexer_12 (
    .in0(in_16), .in1({5{1'b0}}), .out(multiplexer_12_out), .sel(in_2));
  Multiplexer #(.enable("false")) multiplexer_13 (.in0(in_7), .in1(1'b0), .out(multiplexer_13_out), .sel(in_2));
  Register #(.width(32)) register_10 (.D(multiplexer_10_out), .en(in_3), .Q(out_25), .clk(in_1), .clr(in_2));
  Register #(.width(32)) register_11 (.D(multiplexer_11_out), .en(in_3), .Q(out_27), .clk(in_1), .clr(in_2));
  Register #(.width(5)) register_12 (.D(multiplexer_12_out), .en(in_3), .Q(out_29), .clk(in_1), .clr(in_2));
  Register #(.width(1)) register_13 (.D(multiplexer_13_out), .en(in_3), .Q(out_20), .clk(in_1), .clr(in_2));

  // Other names for the same wires on the sheet: CLK = in_1; EN = in_3; RST = in_2
endmodule

module MEM_WB (
  input  in_1,
  input  in_2,
  input  in_3,
  input  in_4,
  input  in_5,
  input  in_6,
  input  in_7,
  input  [31:0] in_8,
  input  [31:0] in_9,
  input  [31:0] in_10,
  input  [4:0] in_11,
  output out_12,
  output out_13,
  output out_14,
  output out_15,
  output [31:0] out_16,
  output [31:0] out_17,
  output [31:0] out_18,
  output [4:0] out_19
);

  wire multiplexer_1_out, multiplexer_6_out, multiplexer_7_out, multiplexer_8_out;
  wire [4:0] multiplexer_5_out;
  wire [31:0] multiplexer_2_out, multiplexer_3_out, multiplexer_4_out;

  Multiplexer #(.enable("false")) multiplexer_1 (.in0(in_4), .in1(1'b0), .out(multiplexer_1_out), .sel(in_2));
  Register #(.width(1)) register_1 (.D(multiplexer_1_out), .en(in_3), .Q(out_12), .clk(in_1), .clr(in_2));
  Register #(.width(32)) register_2 (.D(multiplexer_2_out), .en(in_3), .Q(out_16), .clk(in_1), .clr(in_2));
  Multiplexer #(.width(32), .enable("false")) multiplexer_2 (
    .in0(in_8), .in1({32{1'b0}}), .out(multiplexer_2_out), .sel(in_2));
  Multiplexer #(.width(32), .enable("false")) multiplexer_3 (
    .in0(in_9), .in1({32{1'b0}}), .out(multiplexer_3_out), .sel(in_2));
  Register #(.width(32)) register_3 (.D(multiplexer_3_out), .en(in_3), .Q(out_17), .clk(in_1), .clr(in_2));
  Multiplexer #(.width(32), .enable("false")) multiplexer_4 (
    .in0(in_10), .in1({32{1'b0}}), .out(multiplexer_4_out), .sel(in_2));
  Register #(.width(32)) register_4 (.D(multiplexer_4_out), .en(in_3), .Q(out_18), .clk(in_1), .clr(in_2));
  Multiplexer #(.width(5), .enable("false")) multiplexer_5 (
    .in0(in_11), .in1({5{1'b0}}), .out(multiplexer_5_out), .sel(in_2));
  Register #(.width(5)) register_5 (.D(multiplexer_5_out), .en(in_3), .Q(out_19), .clk(in_1), .clr(in_2));
  Multiplexer #(.enable("false")) multiplexer_6 (.in0(in_5), .in1(1'b0), .out(multiplexer_6_out), .sel(in_2));
  Register #(.width(1)) register_6 (.D(multiplexer_6_out), .en(in_3), .Q(out_13), .clk(in_1), .clr(in_2));
  Multiplexer #(.enable("false")) multiplexer_7 (.in0(in_6), .in1(1'b0), .out(multiplexer_7_out), .sel(in_2));
  Register #(.width(1)) register_7 (.D(multiplexer_7_out), .en(in_3), .Q(out_14), .clk(in_1), .clr(in_2));
  Multiplexer #(.enable("false")) multiplexer_8 (.in0(in_7), .in1(1'b0), .out(multiplexer_8_out), .sel(in_2));
  Register #(.width(1)) register_8 (.D(multiplexer_8_out), .en(in_3), .Q(out_15), .clk(in_1), .clr(in_2));

  // Other names for the same wires on the sheet: CLK = in_1; EN = in_3; RST = in_2
endmodule
